// Logisim project BBCPU.circ as structural Verilog: 2 circuits, main circuit main
module main (
  input  in_1,
  input  in_2,
  input  in_3,
  output out_4,
  output out_5
);

  wire n7404_1_pin2, n7404_1_pin4, n7432_1_pin3, n7432_1_pin6, n7486_1_pin3;

  _7486 u_7486_1 (
    .pin1(in_2), .pin2(in_3), .pin3(n7486_1_pin3), .pin4(n7486_1_pin3), .pin5(in_1), .pin6(out_5));  // open: pin13, pin12, pin11, pin10, pin9, pin8
  _7404 u_7404_1 (
    .pin1(out_5), .pin2(n7404_1_pin2), .pin3(n7486_1_pin3), .pin4(n7404_1_pin4));  // open: pin5, pin6, pin13, pin12, pin11, pin10, pin9, pin8
  _7432 u_7432_1 (
    .pin1(n7404_1_pin2), .pin2(n7404_1_pin4), .pin3(n7432_1_pin3), .pin4(in_2), .pin5(in_3),
    .pin6(n7432_1_pin6));  // open: pin13, pin12, pin11, pin10, pin9, pin8
  _7408 u_7408_1 (
    .pin1(n7432_1_pin3), .pin2(n7432_1_pin6), .pin3(out_4));  // open: pin4, pin5, pin6, pin13, pin12, pin11, pin10, pin9, pin8
endmodule

module OneBitAdder (
  input  A,
  input  B,
  input  CIn,
  output COut,
  output S
);

  wire n7404_1_pin2, n7404_1_pin4, n7432_1_pin3, n7432_1_pin6, n7486_1_pin3;

  _7486 u_7486_1 (
    .pin1(B), .pin2(CIn), .pin3(n7486_1_pin3), .pin4(n7486_1_pin3), .pin5(A), .pin6(S));  // open: pin13, pin12, pin11, pin10, pin9, pin8
  _7404 u_7404_1 (
    .pin1(S), .pin2(n7404_1_pin2), .pin3(n7486_1_pin3), .pin4(n7404_1_pin4));  // open: pin5, pin6, pin13, pin12, pin11, pin10, pin9, pin8
  _7432 u_7432_1 (
    .pin1(n7404_1_pin2), .pin2(n7404_1_pin4), .pin3(n7432_1_pin3), .pin4(B), .pin5(CIn), .pin6(n7432_1_pin6));  // open: pin13, pin12, pin11, pin10, pin9, pin8
  _7408 u_7408_1 (
    .pin1(n7432_1_pin3), .pin2(n7432_1_pin6), .pin3(COut));  // open: pin4, pin5, pin6, pin13, pin12, pin11, pin10, pin9, pin8
endmodule
