// Logisim project CPU.circ as structural Verilog: 29 circuits, main circuit main
module main (
);

  wire clock_1_out, cpu_1_a3, cpu_1_mws, cpu_1_out_11, cpu_1_out_12, cpu_1_out_13, cpu_1_out_15,
       cpu_1_out_16, cpu_1_out_17, cpu_1_w3, sixteenmemorymodule_1_y0, sixteenmemorymodule_1_y1,
       sixteenmemorymodule_1_y2, sixteenmemorymodule_1_y3;
  wire [3:0] cpu_1_x0;

  Clock clock_1 (.out(clock_1_out));
  CPU cpu_1 (
    .CK(clock_1_out), .D3(sixteenmemorymodule_1_y3), .in_3(sixteenmemorymodule_1_y2),
    .in_4(sixteenmemorymodule_1_y1), .in_5(sixteenmemorymodule_1_y0), .X3(cpu_1_x0[3]), .X2(cpu_1_x0[2]),
    .X1(cpu_1_x0[1]), .X0(cpu_1_x0[0]), .A3(cpu_1_a3), .out_11(cpu_1_out_11), .out_12(cpu_1_out_12),
    .out_13(cpu_1_out_13), .W3(cpu_1_w3), .out_15(cpu_1_out_15), .out_16(cpu_1_out_16),
    .out_17(cpu_1_out_17), .MWS(cpu_1_mws));
  Hex_Digit_Display hex_digit_display_1 (.value(cpu_1_x0));  // open: dp
  SixteenMemoryModule sixteenmemorymodule_1 (
    .A3(cpu_1_a3), .A2(cpu_1_out_11), .A1(cpu_1_out_12), .A0(cpu_1_out_13), .D3(cpu_1_w3), .D2(cpu_1_out_15),
    .D1(cpu_1_out_16), .D0(cpu_1_out_17), .S(cpu_1_mws), .CK(clock_1_out), .Y3(sixteenmemorymodule_1_y3),
    .Y2(sixteenmemorymodule_1_y2), .Y1(sixteenmemorymodule_1_y1), .Y0(sixteenmemorymodule_1_y0));
endmodule

module OneBitAdder (
  input  A,
  input  B,
  input  C_in,
  output Sum,
  output C_out
);

  wire not_1_out, not_2_out, or_1_out, or_2_out, xor_1_out;

  xor xor_1 (xor_1_out, B, C_in);
  xor xor_2 (Sum, A, xor_1_out);
  not not_1 (not_1_out, Sum);
  not not_2 (not_2_out, xor_1_out);
  or or_1 (or_1_out, not_1_out, not_2_out);
  or or_2 (or_2_out, B, C_in);
  and and_1 (C_out, or_1_out, or_2_out);
endmodule

module FourBitAdder (
  input  A3,
  input  A2,
  input  A1,
  input  A0,
  input  B3,
  input  B2,
  input  B1,
  input  B0,
  output O,
  output X3,
  output X2,
  output X1,
  output X0
);

  wire onebitadder_2_c_out, onebitadder_3_c_out, onebitadder_4_c_out;

  OneBitAdder onebitadder_1 (.A(A3), .B(B3), .C_in(onebitadder_2_c_out), .Sum(X3), .C_out(O));
  OneBitAdder onebitadder_2 (.A(A2), .B(B2), .C_in(onebitadder_3_c_out), .Sum(X2), .C_out(onebitadder_2_c_out));
  OneBitAdder onebitadder_3 (.A(A1), .B(B1), .C_in(onebitadder_4_c_out), .Sum(X1), .C_out(onebitadder_3_c_out));
  OneBitAdder onebitadder_4 (.A(A0), .B(B0), .Sum(X0), .C_out(onebitadder_4_c_out));  // open: C_in
endmodule

module FourBitInverter (
  input  A3,
  input  A2,
  input  A1,
  input  A0,
  output Y3,
  output Y2,
  output Y1,
  output Y0
);

  not not_1 (Y3, A3);
  not not_2 (Y2, A2);
  not not_3 (Y1, A1);
  not not_4 (Y0, A0);
endmodule

module FourBitSubtractor (
  input  A3,
  input  A2,
  input  A1,
  input  A0,
  input  B3,
  input  B2,
  input  B1,
  input  B0,
  output X3,
  output X2,
  output X1,
  output X0,
  output B
);

  wire fourbitadder_1_x0, fourbitadder_1_x1, fourbitadder_1_x2, fourbitadder_1_x3, fourbitinverter_1_y0,
       fourbitinverter_1_y1, fourbitinverter_1_y2, fourbitinverter_1_y3;

  FourBitInverter fourbitinverter_1 (
    .A3(B3), .A2(B2), .A1(B1), .A0(B0), .Y3(fourbitinverter_1_y3), .Y2(fourbitinverter_1_y2),
    .Y1(fourbitinverter_1_y1), .Y0(fourbitinverter_1_y0));
  FourBitAdder fourbitadder_1 (
    .A3(1'b0), .A2(1'b0), .A1(1'b0), .A0(1'b1), .B3(fourbitinverter_1_y3), .B2(fourbitinverter_1_y2),
    .B1(fourbitinverter_1_y1), .B0(fourbitinverter_1_y0), .X3(fourbitadder_1_x3), .X2(fourbitadder_1_x2),
    .X1(fourbitadder_1_x1), .X0(fourbitadder_1_x0));  // open: O
  FourBitAdder fourbitadder_2 (
    .A3(A3), .A2(A2), .A1(A1), .A0(A0), .B3(fourbitadder_1_x3), .B2(fourbitadder_1_x2),
    .B1(fourbitadder_1_x1), .B0(fourbitadder_1_x0), .X3(X3), .X2(X2), .X1(X1), .X0(X0));  // open: O
endmodule

module FourBitBuffer (
  input  D3,
  input  D2,
  input  D1,
  input  D0,
  input  S,
  output Y3,
  output Y2,
  output Y1,
  output Y0
);

  and and_1 (Y3, D3, S);
  and and_2 (Y2, D2, S);
  and and_3 (Y1, D1, S);
  and and_4 (Y0, D0, S);
endmodule

module ALU (
  input  OP2,
  input  OP1,
  input  OP0,
  input  CK,
  input  A3,
  input  A2,
  input  A1,
  input  A0,
  input  B3,
  input  B2,
  input  B1,
  input  B0,
  output Y3,
  output Y2,
  output Y1,
  output Y0,
  output C,
  output B,
  output WE
);

  wire fourbitadder_1_x0, fourbitadder_1_x1, fourbitadder_1_x2, fourbitadder_1_x3, fourbitbuffer_1_y0,
       fourbitbuffer_1_y1, fourbitbuffer_1_y2, fourbitbuffer_1_y3, fourbitbuffer_2_y0, fourbitbuffer_2_y1,
       fourbitbuffer_2_y2, fourbitbuffer_2_y3, fourbitbuffer_3_y0, fourbitbuffer_3_y1, fourbitbuffer_3_y2,
       fourbitbuffer_3_y3, fourbitbuffer_4_y0, fourbitbuffer_4_y1, fourbitbuffer_4_y2, fourbitbuffer_4_y3,
       fourbitbuffer_5_y0, fourbitbuffer_5_y1, fourbitbuffer_5_y2, fourbitbuffer_5_y3, fourbitbuffer_6_y0,
       fourbitbuffer_6_y1, fourbitbuffer_6_y2, fourbitbuffer_6_y3, fourbitsubtractor_1_x0,
       fourbitsubtractor_1_x1, fourbitsubtractor_1_x2, fourbitsubtractor_1_x3, leftshiftregister_1_y0,
       leftshiftregister_1_y1, leftshiftregister_1_y2, leftshiftregister_1_y3, rightshiftregister_1_y0,
       rightshiftregister_1_y1, rightshiftregister_1_y2, rightshiftregister_1_y3, threetoeightdemux_1_out1,
       threetoeightdemux_1_out2, threetoeightdemux_1_out3, threetoeightdemux_1_out4;

  FourBitBuffer fourbitbuffer_1 (
    .D3(A3), .D2(A2), .D1(A1), .D0(A0), .S(threetoeightdemux_1_out1), .Y3(fourbitbuffer_1_y3),
    .Y2(fourbitbuffer_1_y2), .Y1(fourbitbuffer_1_y1), .Y0(fourbitbuffer_1_y0));
  FourBitBuffer fourbitbuffer_2 (
    .D3(B3), .D2(B2), .D1(B1), .D0(B0), .S(threetoeightdemux_1_out1), .Y3(fourbitbuffer_2_y3),
    .Y2(fourbitbuffer_2_y2), .Y1(fourbitbuffer_2_y1), .Y0(fourbitbuffer_2_y0));
  FourBitBuffer fourbitbuffer_3 (
    .D3(A3), .D2(A2), .D1(A1), .D0(A0), .S(threetoeightdemux_1_out2), .Y3(fourbitbuffer_3_y3),
    .Y2(fourbitbuffer_3_y2), .Y1(fourbitbuffer_3_y1), .Y0(fourbitbuffer_3_y0));
  FourBitBuffer fourbitbuffer_4 (
    .D3(B3), .D2(B2), .D1(B1), .D0(B0), .S(threetoeightdemux_1_out2), .Y3(fourbitbuffer_4_y3),
    .Y2(fourbitbuffer_4_y2), .Y1(fourbitbuffer_4_y1), .Y0(fourbitbuffer_4_y0));
  FourBitBuffer fourbitbuffer_5 (
    .D3(A3), .D2(A2), .D1(A1), .D0(A0), .S(threetoeightdemux_1_out3), .Y3(fourbitbuffer_5_y3),
    .Y2(fourbitbuffer_5_y2), .Y1(fourbitbuffer_5_y1), .Y0(fourbitbuffer_5_y0));
  FourBitBuffer fourbitbuffer_6 (
    .D3(A3), .D2(A2), .D1(A1), .D0(A0), .S(threetoeightdemux_1_out4), .Y3(fourbitbuffer_6_y3),
    .Y2(fourbitbuffer_6_y2), .Y1(fourbitbuffer_6_y1), .Y0(fourbitbuffer_6_y0));
  ThreeToEightDemux threetoeightdemux_1 (
    .IN2(OP2), .IN1(OP1), .IN0(OP0), .OUT1(threetoeightdemux_1_out1), .OUT2(threetoeightdemux_1_out2),
    .OUT3(threetoeightdemux_1_out3), .OUT4(threetoeightdemux_1_out4));  // open: OUT0, OUT5, OUT6, OUT7
  FourBitAdder fourbitadder_1 (
    .A3(fourbitbuffer_1_y3), .A2(fourbitbuffer_1_y2), .A1(fourbitbuffer_1_y1), .A0(fourbitbuffer_1_y0),
    .B3(fourbitbuffer_2_y3), .B2(fourbitbuffer_2_y2), .B1(fourbitbuffer_2_y1), .B0(fourbitbuffer_2_y0),
    .O(C), .X3(fourbitadder_1_x3), .X2(fourbitadder_1_x2), .X1(fourbitadder_1_x1), .X0(fourbitadder_1_x0));
  or or_1 (WE, threetoeightdemux_1_out1, threetoeightdemux_1_out2, threetoeightdemux_1_out3, threetoeightdemux_1_out4);
  FourBitSubtractor fourbitsubtractor_1 (
    .A3(fourbitbuffer_3_y3), .A2(fourbitbuffer_3_y2), .A1(fourbitbuffer_3_y1), .A0(fourbitbuffer_3_y0),
    .B3(fourbitbuffer_4_y3), .B2(fourbitbuffer_4_y2), .B1(fourbitbuffer_4_y1), .B0(fourbitbuffer_4_y0),
    .X3(fourbitsubtractor_1_x3), .X2(fourbitsubtractor_1_x2), .X1(fourbitsubtractor_1_x1),
    .X0(fourbitsubtractor_1_x0));  // open: B
  RightShiftRegister rightshiftregister_1 (
    .A3(fourbitbuffer_5_y3), .A2(fourbitbuffer_5_y2), .A1(fourbitbuffer_5_y1), .A0(fourbitbuffer_5_y0),
    .CK(CK), .Y3(rightshiftregister_1_y3), .Y2(rightshiftregister_1_y2), .Y1(rightshiftregister_1_y1),
    .Y0(rightshiftregister_1_y0));
  LeftShiftRegister leftshiftregister_1 (
    .A3(fourbitbuffer_6_y3), .A2(fourbitbuffer_6_y2), .A1(fourbitbuffer_6_y1), .A0(fourbitbuffer_6_y0),
    .CK(CK), .Y3(leftshiftregister_1_y3), .Y2(leftshiftregister_1_y2), .Y1(leftshiftregister_1_y1),
    .Y0(leftshiftregister_1_y0));
  ThirtyTwoToFourMux thirtytwotofourmux_1 (
    .S2(OP2), .S1(OP1), .S0(OP0), .A3(1'b0), .in_5(1'b0), .in_6(1'b0), .A0(1'b0), .B(fourbitadder_1_x3),
    .in_9(fourbitadder_1_x2), .in_10(fourbitadder_1_x1), .in_11(fourbitadder_1_x0),
    .C(fourbitsubtractor_1_x3), .in_13(fourbitsubtractor_1_x2), .in_14(fourbitsubtractor_1_x1),
    .in_15(fourbitsubtractor_1_x0), .D(rightshiftregister_1_y3), .in_17(rightshiftregister_1_y2),
    .in_18(rightshiftregister_1_y1), .in_19(rightshiftregister_1_y0), .E(leftshiftregister_1_y3),
    .in_21(leftshiftregister_1_y2), .in_22(leftshiftregister_1_y1), .in_23(leftshiftregister_1_y0), .Y3(Y3),
    .Y2(Y2), .Y1(Y1), .Y0(Y0));  // open: F, in_25, in_26, in_27, G, in_29, in_30, in_31, H, in_33, in_34, in_35

  // Notes on the sheet:
  //   Operands
  //   Opcodes
  //   Add and Sub overflow
  //   Results
endmodule

module ThreeToEightDemux (
  input  IN2,
  input  IN1,
  input  IN0,
  output OUT0,
  output OUT1,
  output OUT2,
  output OUT3,
  output OUT4,
  output OUT5,
  output OUT6,
  output OUT7
);

  wire not_1_out, not_2_out, not_3_out, not_4_out, not_5_out, not_6_out, not_7_out, not_8_out, not_9_out,
       not_10_out, not_11_out, not_12_out;

  not not_1 (not_1_out, IN2);
  not not_2 (not_2_out, IN1);
  not not_3 (not_3_out, IN0);
  not not_4 (not_4_out, IN2);
  not not_5 (not_5_out, IN1);
  not not_6 (not_6_out, IN2);
  not not_7 (not_7_out, IN0);
  not not_8 (not_8_out, IN2);
  not not_9 (not_9_out, IN1);
  not not_10 (not_10_out, IN0);
  not not_11 (not_11_out, IN1);
  not not_12 (not_12_out, IN0);
  and and_1 (OUT0, not_1_out, not_2_out, not_3_out);
  and and_2 (OUT1, not_4_out, not_5_out, IN0);
  and and_3 (OUT2, not_6_out, IN1, not_7_out);
  and and_4 (OUT3, not_8_out, IN1, IN0);
  and and_5 (OUT4, IN2, not_9_out, not_10_out);
  and and_6 (OUT5, IN2, not_11_out, IN0);
  and and_7 (OUT6, IN2, IN1, not_12_out);
  and and_8 (OUT7, IN2, IN1, IN0);
endmodule

module ThirtyTwoToFourMux (
  input  S2,
  input  S1,
  input  S0,
  input  A3,
  input  in_5,
  input  in_6,
  input  A0,
  input  B,
  input  in_9,
  input  in_10,
  input  in_11,
  input  C,
  input  in_13,
  input  in_14,
  input  in_15,
  input  D,
  input  in_17,
  input  in_18,
  input  in_19,
  input  E,
  input  in_21,
  input  in_22,
  input  in_23,
  input  F,
  input  in_25,
  input  in_26,
  input  in_27,
  input  G,
  input  in_29,
  input  in_30,
  input  in_31,
  input  H,
  input  in_33,
  input  in_34,
  input  in_35,
  output Y3,
  output Y2,
  output Y1,
  output Y0
);

  wire and_1_out, and_2_out, and_3_out, and_4_out, and_5_out, and_6_out, and_7_out, and_8_out,
       fourbitbuffer_1_y0, fourbitbuffer_1_y1, fourbitbuffer_1_y2, fourbitbuffer_1_y3, fourbitbuffer_2_y0,
       fourbitbuffer_2_y1, fourbitbuffer_2_y2, fourbitbuffer_2_y3, fourbitbuffer_3_y0, fourbitbuffer_3_y1,
       fourbitbuffer_3_y2, fourbitbuffer_3_y3, fourbitbuffer_4_y0, fourbitbuffer_4_y1, fourbitbuffer_4_y2,
       fourbitbuffer_4_y3, fourbitbuffer_5_y0, fourbitbuffer_5_y1, fourbitbuffer_5_y2, fourbitbuffer_5_y3,
       fourbitbuffer_6_y0, fourbitbuffer_6_y1, fourbitbuffer_6_y2, fourbitbuffer_6_y3, fourbitbuffer_7_y0,
       fourbitbuffer_7_y1, fourbitbuffer_7_y2, fourbitbuffer_7_y3, fourbitbuffer_8_y0, fourbitbuffer_8_y1,
       fourbitbuffer_8_y2, fourbitbuffer_8_y3, not_1_out, not_2_out, not_3_out, not_4_out, not_5_out,
       not_6_out, not_7_out, not_8_out, not_9_out, not_10_out, not_11_out, not_12_out;

  not not_1 (not_1_out, S2);
  not not_2 (not_2_out, S1);
  not not_3 (not_3_out, S0);
  not not_4 (not_4_out, S2);
  not not_5 (not_5_out, S1);
  not not_6 (not_6_out, S2);
  not not_7 (not_7_out, S0);
  not not_8 (not_8_out, S2);
  not not_9 (not_9_out, S1);
  not not_10 (not_10_out, S0);
  not not_11 (not_11_out, S1);
  not not_12 (not_12_out, S0);
  and and_1 (and_1_out, not_1_out, not_2_out, not_3_out);
  and and_2 (and_2_out, not_4_out, not_5_out, S0);
  and and_3 (and_3_out, not_6_out, S1, not_7_out);
  and and_4 (and_4_out, not_8_out, S1, S0);
  and and_5 (and_5_out, S2, not_9_out, not_10_out);
  and and_6 (and_6_out, S2, not_11_out, S0);
  and and_7 (and_7_out, S2, S1, not_12_out);
  and and_8 (and_8_out, S2, S1, S0);
  FourBitBuffer fourbitbuffer_1 (
    .D3(A3), .D2(in_5), .D1(in_6), .D0(A0), .S(and_1_out), .Y3(fourbitbuffer_1_y3), .Y2(fourbitbuffer_1_y2),
    .Y1(fourbitbuffer_1_y1), .Y0(fourbitbuffer_1_y0));
  FourBitBuffer fourbitbuffer_2 (
    .D3(B), .D2(in_9), .D1(in_10), .D0(in_11), .S(and_2_out), .Y3(fourbitbuffer_2_y3),
    .Y2(fourbitbuffer_2_y2), .Y1(fourbitbuffer_2_y1), .Y0(fourbitbuffer_2_y0));
  FourBitBuffer fourbitbuffer_3 (
    .D3(C), .D2(in_13), .D1(in_14), .D0(in_15), .S(and_3_out), .Y3(fourbitbuffer_3_y3),
    .Y2(fourbitbuffer_3_y2), .Y1(fourbitbuffer_3_y1), .Y0(fourbitbuffer_3_y0));
  FourBitBuffer fourbitbuffer_4 (
    .D3(D), .D2(in_17), .D1(in_18), .D0(in_19), .S(and_4_out), .Y3(fourbitbuffer_4_y3),
    .Y2(fourbitbuffer_4_y2), .Y1(fourbitbuffer_4_y1), .Y0(fourbitbuffer_4_y0));
  FourBitBuffer fourbitbuffer_5 (
    .D3(E), .D2(in_21), .D1(in_22), .D0(in_23), .S(and_5_out), .Y3(fourbitbuffer_5_y3),
    .Y2(fourbitbuffer_5_y2), .Y1(fourbitbuffer_5_y1), .Y0(fourbitbuffer_5_y0));
  FourBitBuffer fourbitbuffer_6 (
    .D3(F), .D2(in_25), .D1(in_26), .D0(in_27), .S(and_6_out), .Y3(fourbitbuffer_6_y3),
    .Y2(fourbitbuffer_6_y2), .Y1(fourbitbuffer_6_y1), .Y0(fourbitbuffer_6_y0));
  FourBitBuffer fourbitbuffer_7 (
    .D3(G), .D2(in_29), .D1(in_30), .D0(in_31), .S(and_7_out), .Y3(fourbitbuffer_7_y3),
    .Y2(fourbitbuffer_7_y2), .Y1(fourbitbuffer_7_y1), .Y0(fourbitbuffer_7_y0));
  FourBitBuffer fourbitbuffer_8 (
    .D3(H), .D2(in_33), .D1(in_34), .D0(in_35), .S(and_8_out), .Y3(fourbitbuffer_8_y3),
    .Y2(fourbitbuffer_8_y2), .Y1(fourbitbuffer_8_y1), .Y0(fourbitbuffer_8_y0));
  or or_1 (Y3, fourbitbuffer_1_y3, fourbitbuffer_2_y3, fourbitbuffer_3_y3, fourbitbuffer_4_y3, fourbitbuffer_5_y3, fourbitbuffer_6_y3, fourbitbuffer_7_y3, fourbitbuffer_8_y3);
  or or_2 (Y2, fourbitbuffer_1_y2, fourbitbuffer_2_y2, fourbitbuffer_3_y2, fourbitbuffer_4_y2, fourbitbuffer_5_y2, fourbitbuffer_6_y2, fourbitbuffer_7_y2, fourbitbuffer_8_y2);
  or or_3 (Y1, fourbitbuffer_1_y1, fourbitbuffer_2_y1, fourbitbuffer_3_y1, fourbitbuffer_4_y1, fourbitbuffer_5_y1, fourbitbuffer_6_y1, fourbitbuffer_7_y1, fourbitbuffer_8_y1);
  or or_4 (Y0, fourbitbuffer_1_y0, fourbitbuffer_2_y0, fourbitbuffer_3_y0, fourbitbuffer_4_y0, fourbitbuffer_5_y0, fourbitbuffer_6_y0, fourbitbuffer_7_y0, fourbitbuffer_8_y0);
endmodule

module PISORegister (
  input  P3,
  input  P2,
  input  P1,
  input  P0,
  input  S,
  input  CK,
  output SO
);

  wire and_1_out, and_2_out, and_3_out, and_4_out, and_5_out, and_6_out, d_ff_1_q, d_ff_2_q, d_ff_3_q,
       not_1_out, or_1_out, or_2_out, or_3_out;

  not not_1 (not_1_out, S);
  D_Flip_Flop d_ff_1 (.D(P3), .clk(CK), .Q(d_ff_1_q));  // open: Qn, preset, reset
  and and_1 (and_1_out, d_ff_1_q, S);
  and and_2 (and_2_out, not_1_out, P2);
  or or_1 (or_1_out, and_1_out, and_2_out);
  D_Flip_Flop d_ff_2 (.D(or_1_out), .clk(CK), .Q(d_ff_2_q));  // open: Qn, preset, reset
  and and_3 (and_3_out, d_ff_2_q, S);
  and and_4 (and_4_out, not_1_out, P1);
  or or_2 (or_2_out, and_3_out, and_4_out);
  D_Flip_Flop d_ff_3 (.D(or_2_out), .clk(CK), .Q(d_ff_3_q));  // open: Qn, preset, reset
  and and_5 (and_5_out, d_ff_3_q, S);
  and and_6 (and_6_out, not_1_out, P0);
  or or_3 (or_3_out, and_5_out, and_6_out);
  D_Flip_Flop d_ff_4 (.D(or_3_out), .clk(CK), .Q(SO));  // open: Qn, preset, reset
endmodule

module CPU (
  input  CK,
  input  D3,
  input  in_3,
  input  in_4,
  input  in_5,
  output X3,
  output X2,
  output X1,
  output X0,
  output A3,
  output out_11,
  output out_12,
  output out_13,
  output W3,
  output out_15,
  output out_16,
  output out_17,
  output MWS
);

  wire alu_1_we, alu_1_y0, alu_1_y1, alu_1_y2, alu_1_y3, and_1_out, and_2_out, and_3_out, AW0, AW1, AW2, AW3,
       AWS, BW0, BW1, BW2, BW3, BWS, controlunit_1_hlt, controlunit_1_out_61, controlunit_1_out_62,
       controlunit_1_out_63, controlunit_1_out_64, controlunit_1_out_65, controlunit_1_out_66,
       controlunit_1_out_67, controlunit_1_out_68, controlunit_1_out_69, controlunit_1_out_70,
       controlunit_1_out_71, controlunit_1_pcw, controlunit_1_pcw11, MA0, MA1, MA2, MA3, MW0, MW1, MW2, MW3,
       MWS_t, not_1_out, OP0, OP1, OP2, OP3, programcounter_1_out_16, programcounter_1_out_17,
       programcounter_1_out_18, programcounter_1_out_19, programcounter_1_out_20, programcounter_1_out_21,
       programcounter_1_out_22, programcounter_1_out_23, programcounter_1_out_24, programcounter_1_out_25,
       programcounter_1_out_26, programcounter_1_y11, RegisterA_out_7, RegisterA_out_8, RegisterA_out_9,
       RegisterA_out_10, RegisterB_out_7, RegisterB_out_8, RegisterB_out_9, RegisterB_out_10,
       sixteenmemorymodule_1_y0, sixteenmemorymodule_1_y1, sixteenmemorymodule_1_y2, sixteenmemorymodule_1_y3;
  wire [7:0] PROGMEM_data;
  wire [11:0] twelvebitregister_1_out_26;

  ProgramCounter programcounter_1 (
    .S11(controlunit_1_pcw11), .in_2(controlunit_1_out_61), .in_3(controlunit_1_out_62),
    .in_4(controlunit_1_out_63), .in_5(controlunit_1_out_64), .in_6(controlunit_1_out_65),
    .in_7(controlunit_1_out_66), .in_8(controlunit_1_out_67), .in_9(controlunit_1_out_68),
    .in_10(controlunit_1_out_69), .in_11(controlunit_1_out_70), .in_12(controlunit_1_out_71),
    .HALT(controlunit_1_hlt), .CK(CK), .W(controlunit_1_pcw), .out_16(programcounter_1_out_16),
    .out_17(programcounter_1_out_17), .out_18(programcounter_1_out_18), .out_19(programcounter_1_out_19),
    .out_20(programcounter_1_out_20), .out_21(programcounter_1_out_21), .out_22(programcounter_1_out_22),
    .out_23(programcounter_1_out_23), .out_24(programcounter_1_out_24), .out_25(programcounter_1_out_25),
    .out_26(programcounter_1_out_26), .Y11(programcounter_1_y11));
  and and_1 (and_1_out, AWS, OP3);
  and and_2 (and_2_out, BWS, OP3);
  TwelveBitRegister twelvebitregister_1 (
    .W11(programcounter_1_y11), .in_2(programcounter_1_out_26), .in_3(programcounter_1_out_25),
    .in_4(programcounter_1_out_24), .in_5(programcounter_1_out_23), .in_6(programcounter_1_out_22),
    .in_7(programcounter_1_out_21), .in_8(programcounter_1_out_20), .in_9(programcounter_1_out_19),
    .in_10(programcounter_1_out_18), .in_11(programcounter_1_out_17), .in_12(programcounter_1_out_16),
    .W(1'b1), .CK(CK), .D11(twelvebitregister_1_out_26[11]), .out_16(twelvebitregister_1_out_26[10]),
    .out_17(twelvebitregister_1_out_26[9]), .out_18(twelvebitregister_1_out_26[8]),
    .out_19(twelvebitregister_1_out_26[7]), .out_20(twelvebitregister_1_out_26[6]),
    .out_21(twelvebitregister_1_out_26[5]), .out_22(twelvebitregister_1_out_26[4]),
    .out_23(twelvebitregister_1_out_26[3]), .out_24(twelvebitregister_1_out_26[2]),
    .out_25(twelvebitregister_1_out_26[1]), .out_26(twelvebitregister_1_out_26[0]));
  FourBitRegister RegisterA (
    .W3(AW3), .W2(AW2), .W1(AW1), .W0(AW0), .W(and_1_out), .CK(CK), .out_7(RegisterA_out_7),
    .out_8(RegisterA_out_8), .out_9(RegisterA_out_9), .out_10(RegisterA_out_10));
  FourBitRegister RegisterB (
    .W3(BW3), .W2(BW2), .W1(BW1), .W0(BW0), .W(and_2_out), .CK(CK), .out_7(RegisterB_out_7),
    .out_8(RegisterB_out_8), .out_9(RegisterB_out_9), .out_10(RegisterB_out_10));
  ROM #(.addrWidth(12), .dataWidth(12)) PROGMEM (
    .addr(twelvebitregister_1_out_26), .data({OP3, OP2, OP1, OP0, PROGMEM_data}));
  ControlUnit controlunit_1 (
    .S2(OP2), .S1(OP1), .S0(OP0), .AR(RegisterA_out_7), .in_5(RegisterA_out_8), .in_6(RegisterA_out_9),
    .in_7(RegisterA_out_10), .BR(RegisterB_out_7), .in_9(RegisterB_out_8), .in_10(RegisterB_out_9),
    .in_11(RegisterB_out_10), .XR(X3), .in_13(X2), .in_14(X1), .in_15(X0), .OPA(PROGMEM_data[7]),
    .in_17(PROGMEM_data[6]), .in_18(PROGMEM_data[5]), .in_19(PROGMEM_data[4]), .OPB(PROGMEM_data[3]),
    .in_21(PROGMEM_data[2]), .in_22(PROGMEM_data[1]), .in_23(PROGMEM_data[0]),
    .PC11(twelvebitregister_1_out_26[11]), .in_25(twelvebitregister_1_out_26[10]),
    .in_26(twelvebitregister_1_out_26[9]), .in_27(twelvebitregister_1_out_26[8]),
    .in_28(twelvebitregister_1_out_26[7]), .in_29(twelvebitregister_1_out_26[6]),
    .in_30(twelvebitregister_1_out_26[5]), .in_31(twelvebitregister_1_out_26[4]),
    .in_32(twelvebitregister_1_out_26[3]), .in_33(twelvebitregister_1_out_26[2]),
    .in_34(twelvebitregister_1_out_26[1]), .in_35(twelvebitregister_1_out_26[0]),
    .MD(sixteenmemorymodule_1_y3), .in_37(sixteenmemorymodule_1_y2), .in_38(sixteenmemorymodule_1_y1),
    .in_39(sixteenmemorymodule_1_y0), .CK(CK), .AW(AW3), .out_42(AW2), .out_43(AW1), .out_44(AW0), .AWS(AWS),
    .BW(BW3), .out_47(BW2), .out_48(BW1), .out_49(BW0), .BWS(BWS), .MA(MA3), .out_52(MA2), .out_53(MA1),
    .out_54(MA0), .MW(MW3), .out_56(MW2), .out_57(MW1), .out_58(MW0), .MWS(MWS_t),
    .PCW11(controlunit_1_pcw11), .out_61(controlunit_1_out_61), .out_62(controlunit_1_out_62),
    .out_63(controlunit_1_out_63), .out_64(controlunit_1_out_64), .out_65(controlunit_1_out_65),
    .out_66(controlunit_1_out_66), .out_67(controlunit_1_out_67), .out_68(controlunit_1_out_68),
    .out_69(controlunit_1_out_69), .out_70(controlunit_1_out_70), .out_71(controlunit_1_out_71),
    .PCW(controlunit_1_pcw), .HLT(controlunit_1_hlt));
  ALU alu_1 (
    .OP2(OP2), .OP1(OP1), .OP0(OP0), .CK(CK), .A3(RegisterA_out_7), .A2(RegisterA_out_8),
    .A1(RegisterA_out_9), .A0(RegisterA_out_10), .B3(RegisterB_out_7), .B2(RegisterB_out_8),
    .B1(RegisterB_out_9), .B0(RegisterB_out_10), .Y3(alu_1_y3), .Y2(alu_1_y2), .Y1(alu_1_y1), .Y0(alu_1_y0),
    .WE(alu_1_we));  // open: C, B
  and and_3 (and_3_out, alu_1_we, not_1_out);
  not not_1 (not_1_out, OP3);
  SixteenMemoryModule sixteenmemorymodule_1 (
    .A3(MA3), .A2(MA2), .A1(MA1), .A0(MA0), .D3(MW3), .D2(MW2), .D1(MW1), .D0(MW0), .S(MWS_t), .CK(CK),
    .Y3(sixteenmemorymodule_1_y3), .Y2(sixteenmemorymodule_1_y2), .Y1(sixteenmemorymodule_1_y1),
    .Y0(sixteenmemorymodule_1_y0));
  FourBitRegister Accumulator (
    .W3(alu_1_y3), .W2(alu_1_y2), .W1(alu_1_y1), .W0(alu_1_y0), .W(and_3_out), .CK(CK), .out_7(X3),
    .out_8(X2), .out_9(X1), .out_10(X0));
  Hex_Digit_Display hex_digit_display_1 (.value({X3, X2, X1, X0}));  // open: dp

  // Notes on the sheet:
  //   may need to create an 2 clock pulse cycle - one for loading instruction and another for execution.
  //   put CK when done testing
  //   we dont want register write on 0000 (idle op)
  //   problem: registers dont hold for more than a cpu cycle
  //   contents of PROGMEM (hex, n*v repeats v):
  //   930 100 c00 920 100 c10 a20 0 800 a10 0 200 df0 a00 0 800 a30 0 100 c30 901 a20 0 100 c20 bf3
  //   might have to add the instruction register after accessing rom instead of befoire
  //   JMZ jump if zero operation uses the value of the accumulator to check zero, then changes program counter as usual
endmodule

module DataStore (
  input  A3,
  input  A2,
  input  A1,
  input  A0,
  input  CK,
  output Y3,
  output Y2,
  output Y1,
  output Y0
);

  D_Flip_Flop d_ff_1 (.D(A3), .clk(CK), .Q(Y3));  // open: Qn, preset, reset
  D_Flip_Flop d_ff_2 (.D(A2), .clk(CK), .Q(Y2));  // open: Qn, preset, reset
  D_Flip_Flop d_ff_3 (.D(A1), .clk(CK), .Q(Y1));  // open: Qn, preset, reset
  D_Flip_Flop d_ff_4 (.D(A0), .clk(CK), .Q(Y0));  // open: Qn, preset, reset
endmodule

module RightShiftRegister (
  input  A3,
  input  A2,
  input  A1,
  input  A0,
  input  CK,
  output Y3,
  output Y2,
  output Y1,
  output Y0
);

  D_Flip_Flop d_ff_1 (.D(1'b0), .clk(CK), .Q(Y3));  // open: Qn, preset, reset
  D_Flip_Flop d_ff_2 (.D(A3), .clk(CK), .Q(Y2));  // open: Qn, preset, reset
  // NoConnect on A0
  D_Flip_Flop d_ff_3 (.D(A2), .clk(CK), .Q(Y1));  // open: Qn, preset, reset
  D_Flip_Flop d_ff_4 (.D(A1), .clk(CK), .Q(Y0));  // open: Qn, preset, reset
endmodule

module LeftShiftRegister (
  input  A3,
  input  A2,
  input  A1,
  input  A0,
  input  CK,
  output Y3,
  output Y2,
  output Y1,
  output Y0
);

  D_Flip_Flop d_ff_1 (.D(A2), .clk(CK), .Q(Y3));  // open: Qn, preset, reset
  // NoConnect on A3
  D_Flip_Flop d_ff_2 (.D(A1), .clk(CK), .Q(Y2));  // open: Qn, preset, reset
  D_Flip_Flop d_ff_3 (.D(A0), .clk(CK), .Q(Y1));  // open: Qn, preset, reset
  D_Flip_Flop d_ff_4 (.D(1'b0), .clk(CK), .Q(Y0));  // open: Qn, preset, reset
endmodule

module SixteenMemoryModule (
  input  A3,
  input  A2,
  input  A1,
  input  A0,
  input  D3,
  input  D2,
  input  D1,
  input  D0,
  input  S,
  input  CK,
  output Y3,
  output Y2,
  output Y1,
  output Y0
);

  wire RegisterEight_out_7, RegisterEight_out_8, RegisterEight_out_9, RegisterEight_out_10,
       RegisterEleven_out_7, RegisterEleven_out_8, RegisterEleven_out_9, RegisterEleven_out_10,
       RegisterFifteen_out_7, RegisterFifteen_out_8, RegisterFifteen_out_9, RegisterFifteen_out_10,
       RegisterFive_out_7, RegisterFive_out_8, RegisterFive_out_9, RegisterFive_out_10, RegisterFour_out_7,
       RegisterFour_out_8, RegisterFour_out_9, RegisterFour_out_10, RegisterFourteen_out_7,
       RegisterFourteen_out_8, RegisterFourteen_out_9, RegisterFourteen_out_10, RegisterNine_out_7,
       RegisterNine_out_8, RegisterNine_out_9, RegisterNine_out_10, RegisterOne_out_7, RegisterOne_out_8,
       RegisterOne_out_9, RegisterOne_out_10, RegisterSeven_out_7, RegisterSeven_out_8, RegisterSeven_out_9,
       RegisterSeven_out_10, RegisterSix_out_7, RegisterSix_out_8, RegisterSix_out_9, RegisterSix_out_10,
       RegisterSixteen_out_7, RegisterSixteen_out_8, RegisterSixteen_out_9, RegisterSixteen_out_10,
       RegisterTen_out_7, RegisterTen_out_8, RegisterTen_out_9, RegisterTen_out_10, RegisterThirteen_out_7,
       RegisterThirteen_out_8, RegisterThirteen_out_9, RegisterThirteen_out_10, RegisterThree_out_7,
       RegisterThree_out_8, RegisterThree_out_9, RegisterThree_out_10, RegisterTwelve_out_7,
       RegisterTwelve_out_8, RegisterTwelve_out_9, RegisterTwelve_out_10, RegisterTwo_out_7,
       RegisterTwo_out_8, RegisterTwo_out_9, RegisterTwo_out_10, W1, W2, W3, W4, W5, W6, W7, W8, W9, W10,
       W11, W12, W13, W14, W15, W16, WR1, WR2, WR3, WR4, WR5, WR6, WR7, WR8, WR9, WR10, WR11, WR12, WR13,
       WR14, WR15, WR16;

  and and_1 (WR1, S, W1);
  and and_2 (WR2, S, W2);
  and and_3 (WR3, S, W3);
  and and_4 (WR4, S, W4);
  and and_5 (WR5, S, W5);
  and and_6 (WR6, S, W6);
  and and_7 (WR7, S, W7);
  and and_8 (WR8, S, W8);
  and and_9 (WR9, S, W9);
  and and_10 (WR10, S, W10);
  and and_11 (WR11, S, W11);
  and and_12 (WR12, S, W12);
  and and_13 (WR13, S, W13);
  and and_14 (WR14, S, W14);
  and and_15 (WR15, S, W15);
  and and_16 (WR16, S, W16);
  FourToSixteenDemux fourtosixteendemux_1 (
    .S3(A3), .S2(A2), .S1(A1), .S0(A0), .out_5(W1), .out_6(W2), .out_7(W3), .out_8(W4), .out_9(W5),
    .out_10(W6), .out_11(W7), .out_12(W8), .out_13(W9), .out_14(W10), .out_15(W11), .out_16(W12),
    .out_17(W13), .out_18(W14), .out_19(W15), .out_20(W16));
  FourBitRegister RegisterOne (
    .W3(D3), .W2(D2), .W1(D1), .W0(D0), .W(WR1), .CK(CK), .out_7(RegisterOne_out_7),
    .out_8(RegisterOne_out_8), .out_9(RegisterOne_out_9), .out_10(RegisterOne_out_10));
  FourBitRegister RegisterFive (
    .W3(D3), .W2(D2), .W1(D1), .W0(D0), .W(WR5), .CK(CK), .out_7(RegisterFive_out_7),
    .out_8(RegisterFive_out_8), .out_9(RegisterFive_out_9), .out_10(RegisterFive_out_10));
  FourBitRegister RegisterNine (
    .W3(D3), .W2(D2), .W1(D1), .W0(D0), .W(WR9), .CK(CK), .out_7(RegisterNine_out_7),
    .out_8(RegisterNine_out_8), .out_9(RegisterNine_out_9), .out_10(RegisterNine_out_10));
  FourBitRegister RegisterThirteen (
    .W3(D3), .W2(D2), .W1(D1), .W0(D0), .W(WR13), .CK(CK), .out_7(RegisterThirteen_out_7),
    .out_8(RegisterThirteen_out_8), .out_9(RegisterThirteen_out_9), .out_10(RegisterThirteen_out_10));
  FourBitRegister RegisterTwo (
    .W3(D3), .W2(D2), .W1(D1), .W0(D0), .W(WR2), .CK(CK), .out_7(RegisterTwo_out_7),
    .out_8(RegisterTwo_out_8), .out_9(RegisterTwo_out_9), .out_10(RegisterTwo_out_10));
  FourBitRegister RegisterSix (
    .W3(D3), .W2(D2), .W1(D1), .W0(D0), .W(WR6), .CK(CK), .out_7(RegisterSix_out_7),
    .out_8(RegisterSix_out_8), .out_9(RegisterSix_out_9), .out_10(RegisterSix_out_10));
  FourBitRegister RegisterTen (
    .W3(D3), .W2(D2), .W1(D1), .W0(D0), .W(WR10), .CK(CK), .out_7(RegisterTen_out_7),
    .out_8(RegisterTen_out_8), .out_9(RegisterTen_out_9), .out_10(RegisterTen_out_10));
  FourBitRegister RegisterFourteen (
    .W3(D3), .W2(D2), .W1(D1), .W0(D0), .W(WR14), .CK(CK), .out_7(RegisterFourteen_out_7),
    .out_8(RegisterFourteen_out_8), .out_9(RegisterFourteen_out_9), .out_10(RegisterFourteen_out_10));
  FourBitRegister RegisterThree (
    .W3(D3), .W2(D2), .W1(D1), .W0(D0), .W(WR3), .CK(CK), .out_7(RegisterThree_out_7),
    .out_8(RegisterThree_out_8), .out_9(RegisterThree_out_9), .out_10(RegisterThree_out_10));
  FourBitRegister RegisterSeven (
    .W3(D3), .W2(D2), .W1(D1), .W0(D0), .W(WR7), .CK(CK), .out_7(RegisterSeven_out_7),
    .out_8(RegisterSeven_out_8), .out_9(RegisterSeven_out_9), .out_10(RegisterSeven_out_10));
  FourBitRegister RegisterEleven (
    .W3(D3), .W2(D2), .W1(D1), .W0(D0), .W(WR11), .CK(CK), .out_7(RegisterEleven_out_7),
    .out_8(RegisterEleven_out_8), .out_9(RegisterEleven_out_9), .out_10(RegisterEleven_out_10));
  FourBitRegister RegisterFifteen (
    .W3(D3), .W2(D2), .W1(D1), .W0(D0), .W(WR15), .CK(CK), .out_7(RegisterFifteen_out_7),
    .out_8(RegisterFifteen_out_8), .out_9(RegisterFifteen_out_9), .out_10(RegisterFifteen_out_10));
  FourBitRegister RegisterFour (
    .W3(D3), .W2(D2), .W1(D1), .W0(D0), .W(WR4), .CK(CK), .out_7(RegisterFour_out_7),
    .out_8(RegisterFour_out_8), .out_9(RegisterFour_out_9), .out_10(RegisterFour_out_10));
  FourBitRegister RegisterEight (
    .W3(D3), .W2(D2), .W1(D1), .W0(D0), .W(WR8), .CK(CK), .out_7(RegisterEight_out_7),
    .out_8(RegisterEight_out_8), .out_9(RegisterEight_out_9), .out_10(RegisterEight_out_10));
  FourBitRegister RegisterTwelve (
    .W3(D3), .W2(D2), .W1(D1), .W0(D0), .W(WR12), .CK(CK), .out_7(RegisterTwelve_out_7),
    .out_8(RegisterTwelve_out_8), .out_9(RegisterTwelve_out_9), .out_10(RegisterTwelve_out_10));
  FourBitRegister RegisterSixteen (
    .W3(D3), .W2(D2), .W1(D1), .W0(D0), .W(WR16), .CK(CK), .out_7(RegisterSixteen_out_7),
    .out_8(RegisterSixteen_out_8), .out_9(RegisterSixteen_out_9), .out_10(RegisterSixteen_out_10));
  SixtyFourToFourMux sixtyfourtofourmux_1 (
    .S3(A3), .S2(A2), .S1(A1), .S0(A0), .A(RegisterOne_out_7), .in_6(RegisterOne_out_8),
    .in_7(RegisterOne_out_9), .in_8(RegisterOne_out_10), .B(RegisterTwo_out_7), .in_10(RegisterTwo_out_8),
    .in_11(RegisterTwo_out_9), .in_12(RegisterTwo_out_10), .C(RegisterThree_out_7),
    .in_14(RegisterThree_out_8), .in_15(RegisterThree_out_9), .in_16(RegisterThree_out_10),
    .D(RegisterFour_out_7), .in_18(RegisterFour_out_8), .in_19(RegisterFour_out_9),
    .in_20(RegisterFour_out_10), .E(RegisterFive_out_7), .in_22(RegisterFive_out_8),
    .in_23(RegisterFive_out_9), .in_24(RegisterFive_out_10), .F(RegisterSix_out_7),
    .in_26(RegisterSix_out_8), .in_27(RegisterSix_out_9), .in_28(RegisterSix_out_10),
    .G(RegisterSeven_out_7), .in_30(RegisterSeven_out_8), .in_31(RegisterSeven_out_9),
    .in_32(RegisterSeven_out_10), .H(RegisterEight_out_7), .in_34(RegisterEight_out_8),
    .in_35(RegisterEight_out_9), .in_36(RegisterEight_out_10), .I(RegisterNine_out_7),
    .in_38(RegisterNine_out_8), .in_39(RegisterNine_out_9), .in_40(RegisterNine_out_10),
    .J(RegisterTen_out_7), .in_42(RegisterTen_out_8), .in_43(RegisterTen_out_9), .in_44(RegisterTen_out_10),
    .K(RegisterEleven_out_7), .in_46(RegisterEleven_out_8), .in_47(RegisterEleven_out_9),
    .in_48(RegisterEleven_out_10), .L(RegisterTwelve_out_7), .in_50(RegisterTwelve_out_8),
    .in_51(RegisterTwelve_out_9), .in_52(RegisterTwelve_out_10), .M(RegisterThirteen_out_7),
    .in_54(RegisterThirteen_out_8), .in_55(RegisterThirteen_out_9), .in_56(RegisterThirteen_out_10),
    .N(RegisterFourteen_out_7), .in_58(RegisterFourteen_out_8), .in_59(RegisterFourteen_out_9),
    .in_60(RegisterFourteen_out_10), .O(RegisterFifteen_out_7), .in_62(RegisterFifteen_out_8),
    .in_63(RegisterFifteen_out_9), .in_64(RegisterFifteen_out_10), .P(RegisterSixteen_out_7),
    .in_66(RegisterSixteen_out_8), .in_67(RegisterSixteen_out_9), .in_68(RegisterSixteen_out_10), .Y3(Y3),
    .Y2(Y2), .Y1(Y1), .Y0(Y0));

  // Other names for the same wires on the sheet: W = S

  // Notes on the sheet:
  //   Address
  //   Data In
  //   Mode Select
  //   ahhhh this is annoying. there is a split second where the address is 0 from before and the w activates ahhhh
  //   may need to add a register for A and D to propagate
  //   Idea: contribute autocomplete labels and tunnels to Logisim.
  //   1-4
  //   5-8
  //   9-12
  //   13-16
endmodule

module FourBitRegister (
  input  W3,
  input  W2,
  input  W1,
  input  W0,
  input  W,
  input  CK,
  output out_7,
  output out_8,
  output out_9,
  output out_10
);

  wire and_1_out, fourbitbuffer_1_y0, fourbitbuffer_1_y1, fourbitbuffer_1_y2, fourbitbuffer_1_y3;

  and and_1 (and_1_out, W, CK);
  FourBitBuffer fourbitbuffer_1 (
    .D3(W3), .D2(W2), .D1(W1), .D0(W0), .S(W), .Y3(fourbitbuffer_1_y3), .Y2(fourbitbuffer_1_y2),
    .Y1(fourbitbuffer_1_y1), .Y0(fourbitbuffer_1_y0));
  DataStore datastore_1 (
    .A3(fourbitbuffer_1_y3), .A2(fourbitbuffer_1_y2), .A1(fourbitbuffer_1_y1), .A0(fourbitbuffer_1_y0),
    .CK(and_1_out), .Y3(out_7), .Y2(out_8), .Y1(out_9), .Y0(out_10));
endmodule

module SixtyFourToFourMux (
  input  S3,
  input  S2,
  input  S1,
  input  S0,
  input  A,
  input  in_6,
  input  in_7,
  input  in_8,
  input  B,
  input  in_10,
  input  in_11,
  input  in_12,
  input  C,
  input  in_14,
  input  in_15,
  input  in_16,
  input  D,
  input  in_18,
  input  in_19,
  input  in_20,
  input  E,
  input  in_22,
  input  in_23,
  input  in_24,
  input  F,
  input  in_26,
  input  in_27,
  input  in_28,
  input  G,
  input  in_30,
  input  in_31,
  input  in_32,
  input  H,
  input  in_34,
  input  in_35,
  input  in_36,
  input  I,
  input  in_38,
  input  in_39,
  input  in_40,
  input  J,
  input  in_42,
  input  in_43,
  input  in_44,
  input  K,
  input  in_46,
  input  in_47,
  input  in_48,
  input  L,
  input  in_50,
  input  in_51,
  input  in_52,
  input  M,
  input  in_54,
  input  in_55,
  input  in_56,
  input  N,
  input  in_58,
  input  in_59,
  input  in_60,
  input  O,
  input  in_62,
  input  in_63,
  input  in_64,
  input  P,
  input  in_66,
  input  in_67,
  input  in_68,
  output Y3,
  output Y2,
  output Y1,
  output Y0
);

  wire and_1_out, and_2_out, and_3_out, and_4_out, and_5_out, and_6_out, and_7_out, and_8_out, and_9_out,
       and_10_out, and_11_out, and_12_out, and_13_out, and_14_out, and_15_out, and_16_out,
       fourbitbuffer_1_y0, fourbitbuffer_1_y1, fourbitbuffer_1_y2, fourbitbuffer_1_y3, fourbitbuffer_2_y0,
       fourbitbuffer_2_y1, fourbitbuffer_2_y2, fourbitbuffer_2_y3, fourbitbuffer_3_y0, fourbitbuffer_3_y1,
       fourbitbuffer_3_y2, fourbitbuffer_3_y3, fourbitbuffer_4_y0, fourbitbuffer_4_y1, fourbitbuffer_4_y2,
       fourbitbuffer_4_y3, fourbitbuffer_5_y0, fourbitbuffer_5_y1, fourbitbuffer_5_y2, fourbitbuffer_5_y3,
       fourbitbuffer_6_y0, fourbitbuffer_6_y1, fourbitbuffer_6_y2, fourbitbuffer_6_y3, fourbitbuffer_7_y0,
       fourbitbuffer_7_y1, fourbitbuffer_7_y2, fourbitbuffer_7_y3, fourbitbuffer_8_y0, fourbitbuffer_8_y1,
       fourbitbuffer_8_y2, fourbitbuffer_8_y3, fourbitbuffer_9_y0, fourbitbuffer_9_y1, fourbitbuffer_9_y2,
       fourbitbuffer_9_y3, fourbitbuffer_10_y0, fourbitbuffer_10_y1, fourbitbuffer_10_y2,
       fourbitbuffer_10_y3, fourbitbuffer_11_y0, fourbitbuffer_11_y1, fourbitbuffer_11_y2,
       fourbitbuffer_11_y3, fourbitbuffer_12_y0, fourbitbuffer_12_y1, fourbitbuffer_12_y2,
       fourbitbuffer_12_y3, fourbitbuffer_13_y0, fourbitbuffer_13_y1, fourbitbuffer_13_y2,
       fourbitbuffer_13_y3, fourbitbuffer_14_y0, fourbitbuffer_14_y1, fourbitbuffer_14_y2,
       fourbitbuffer_14_y3, fourbitbuffer_15_y0, fourbitbuffer_15_y1, fourbitbuffer_15_y2,
       fourbitbuffer_15_y3, fourbitbuffer_16_y0, fourbitbuffer_16_y1, fourbitbuffer_16_y2,
       fourbitbuffer_16_y3, not_1_out, not_2_out, not_3_out, not_4_out, not_5_out, not_6_out, not_7_out,
       not_8_out, not_9_out, not_10_out, not_11_out, not_12_out, not_13_out, not_14_out, not_15_out,
       not_16_out, not_17_out, not_18_out, not_19_out, not_20_out, not_21_out, not_22_out, not_23_out,
       not_24_out, not_25_out, not_26_out, not_27_out, not_28_out, not_29_out, not_30_out, not_31_out,
       not_32_out;

  not not_1 (not_1_out, S2);
  not not_2 (not_2_out, S1);
  not not_3 (not_3_out, S0);
  not not_4 (not_4_out, S2);
  not not_5 (not_5_out, S1);
  not not_6 (not_6_out, S2);
  not not_7 (not_7_out, S0);
  not not_8 (not_8_out, S2);
  not not_9 (not_9_out, S1);
  not not_10 (not_10_out, S0);
  not not_11 (not_11_out, S1);
  not not_12 (not_12_out, S0);
  not not_13 (not_13_out, S3);
  not not_14 (not_14_out, S2);
  not not_15 (not_15_out, S1);
  not not_16 (not_16_out, S0);
  not not_17 (not_17_out, S3);
  not not_18 (not_18_out, S2);
  not not_19 (not_19_out, S1);
  not not_20 (not_20_out, S3);
  not not_21 (not_21_out, S2);
  not not_22 (not_22_out, S0);
  not not_23 (not_23_out, S3);
  not not_24 (not_24_out, S2);
  not not_25 (not_25_out, S3);
  not not_26 (not_26_out, S1);
  not not_27 (not_27_out, S0);
  not not_28 (not_28_out, S3);
  not not_29 (not_29_out, S1);
  not not_30 (not_30_out, S3);
  not not_31 (not_31_out, S0);
  not not_32 (not_32_out, S3);
  and and_1 (and_1_out, not_13_out, not_14_out, not_15_out, not_16_out);
  and and_2 (and_2_out, not_17_out, not_18_out, not_19_out, S0);
  and and_3 (and_3_out, not_20_out, not_21_out, S1, not_22_out);
  and and_4 (and_4_out, not_23_out, not_24_out, S1, S0);
  and and_5 (and_5_out, not_25_out, S2, not_26_out, not_27_out);
  and and_6 (and_6_out, not_28_out, S2, not_29_out, S0);
  and and_7 (and_7_out, not_30_out, S2, S1, not_31_out);
  and and_8 (and_8_out, not_32_out, S2, S1, S0);
  and and_9 (and_9_out, S3, not_1_out, not_2_out, not_3_out);
  and and_10 (and_10_out, S3, not_4_out, not_5_out, S0);
  and and_11 (and_11_out, S3, not_6_out, S1, not_7_out);
  and and_12 (and_12_out, S3, not_8_out, S1, S0);
  and and_13 (and_13_out, S3, S2, not_9_out, not_10_out);
  and and_14 (and_14_out, S3, S2, not_11_out, S0);
  and and_15 (and_15_out, S3, S2, S1, not_12_out);
  and and_16 (and_16_out, S3, S2, S1, S0);
  FourBitBuffer fourbitbuffer_1 (
    .D3(A), .D2(in_6), .D1(in_7), .D0(in_8), .S(and_1_out), .Y3(fourbitbuffer_1_y3), .Y2(fourbitbuffer_1_y2),
    .Y1(fourbitbuffer_1_y1), .Y0(fourbitbuffer_1_y0));
  FourBitBuffer fourbitbuffer_2 (
    .D3(B), .D2(in_10), .D1(in_11), .D0(in_12), .S(and_2_out), .Y3(fourbitbuffer_2_y3),
    .Y2(fourbitbuffer_2_y2), .Y1(fourbitbuffer_2_y1), .Y0(fourbitbuffer_2_y0));
  FourBitBuffer fourbitbuffer_3 (
    .D3(C), .D2(in_14), .D1(in_15), .D0(in_16), .S(and_3_out), .Y3(fourbitbuffer_3_y3),
    .Y2(fourbitbuffer_3_y2), .Y1(fourbitbuffer_3_y1), .Y0(fourbitbuffer_3_y0));
  FourBitBuffer fourbitbuffer_4 (
    .D3(D), .D2(in_18), .D1(in_19), .D0(in_20), .S(and_4_out), .Y3(fourbitbuffer_4_y3),
    .Y2(fourbitbuffer_4_y2), .Y1(fourbitbuffer_4_y1), .Y0(fourbitbuffer_4_y0));
  FourBitBuffer fourbitbuffer_5 (
    .D3(E), .D2(in_22), .D1(in_23), .D0(in_24), .S(and_5_out), .Y3(fourbitbuffer_5_y3),
    .Y2(fourbitbuffer_5_y2), .Y1(fourbitbuffer_5_y1), .Y0(fourbitbuffer_5_y0));
  FourBitBuffer fourbitbuffer_6 (
    .D3(F), .D2(in_26), .D1(in_27), .D0(in_28), .S(and_6_out), .Y3(fourbitbuffer_6_y3),
    .Y2(fourbitbuffer_6_y2), .Y1(fourbitbuffer_6_y1), .Y0(fourbitbuffer_6_y0));
  FourBitBuffer fourbitbuffer_7 (
    .D3(G), .D2(in_30), .D1(in_31), .D0(in_32), .S(and_7_out), .Y3(fourbitbuffer_7_y3),
    .Y2(fourbitbuffer_7_y2), .Y1(fourbitbuffer_7_y1), .Y0(fourbitbuffer_7_y0));
  FourBitBuffer fourbitbuffer_8 (
    .D3(H), .D2(in_34), .D1(in_35), .D0(in_36), .S(and_8_out), .Y3(fourbitbuffer_8_y3),
    .Y2(fourbitbuffer_8_y2), .Y1(fourbitbuffer_8_y1), .Y0(fourbitbuffer_8_y0));
  FourBitBuffer fourbitbuffer_9 (
    .D3(I), .D2(in_38), .D1(in_39), .D0(in_40), .S(and_9_out), .Y3(fourbitbuffer_9_y3),
    .Y2(fourbitbuffer_9_y2), .Y1(fourbitbuffer_9_y1), .Y0(fourbitbuffer_9_y0));
  FourBitBuffer fourbitbuffer_10 (
    .D3(J), .D2(in_42), .D1(in_43), .D0(in_44), .S(and_10_out), .Y3(fourbitbuffer_10_y3),
    .Y2(fourbitbuffer_10_y2), .Y1(fourbitbuffer_10_y1), .Y0(fourbitbuffer_10_y0));
  FourBitBuffer fourbitbuffer_11 (
    .D3(K), .D2(in_46), .D1(in_47), .D0(in_48), .S(and_11_out), .Y3(fourbitbuffer_11_y3),
    .Y2(fourbitbuffer_11_y2), .Y1(fourbitbuffer_11_y1), .Y0(fourbitbuffer_11_y0));
  FourBitBuffer fourbitbuffer_12 (
    .D3(L), .D2(in_50), .D1(in_51), .D0(in_52), .S(and_12_out), .Y3(fourbitbuffer_12_y3),
    .Y2(fourbitbuffer_12_y2), .Y1(fourbitbuffer_12_y1), .Y0(fourbitbuffer_12_y0));
  FourBitBuffer fourbitbuffer_13 (
    .D3(M), .D2(in_54), .D1(in_55), .D0(in_56), .S(and_13_out), .Y3(fourbitbuffer_13_y3),
    .Y2(fourbitbuffer_13_y2), .Y1(fourbitbuffer_13_y1), .Y0(fourbitbuffer_13_y0));
  FourBitBuffer fourbitbuffer_14 (
    .D3(N), .D2(in_58), .D1(in_59), .D0(in_60), .S(and_14_out), .Y3(fourbitbuffer_14_y3),
    .Y2(fourbitbuffer_14_y2), .Y1(fourbitbuffer_14_y1), .Y0(fourbitbuffer_14_y0));
  FourBitBuffer fourbitbuffer_15 (
    .D3(O), .D2(in_62), .D1(in_63), .D0(in_64), .S(and_15_out), .Y3(fourbitbuffer_15_y3),
    .Y2(fourbitbuffer_15_y2), .Y1(fourbitbuffer_15_y1), .Y0(fourbitbuffer_15_y0));
  FourBitBuffer fourbitbuffer_16 (
    .D3(P), .D2(in_66), .D1(in_67), .D0(in_68), .S(and_16_out), .Y3(fourbitbuffer_16_y3),
    .Y2(fourbitbuffer_16_y2), .Y1(fourbitbuffer_16_y1), .Y0(fourbitbuffer_16_y0));
  or or_1 (Y3, fourbitbuffer_1_y3, fourbitbuffer_2_y3, fourbitbuffer_3_y3, fourbitbuffer_4_y3, fourbitbuffer_5_y3, fourbitbuffer_6_y3, fourbitbuffer_7_y3, fourbitbuffer_8_y3, fourbitbuffer_9_y3, fourbitbuffer_10_y3, fourbitbuffer_11_y3, fourbitbuffer_12_y3, fourbitbuffer_13_y3, fourbitbuffer_14_y3, fourbitbuffer_15_y3, fourbitbuffer_16_y3);
  or or_2 (Y2, fourbitbuffer_1_y2, fourbitbuffer_2_y2, fourbitbuffer_3_y2, fourbitbuffer_4_y2, fourbitbuffer_5_y2, fourbitbuffer_6_y2, fourbitbuffer_7_y2, fourbitbuffer_8_y2, fourbitbuffer_9_y2, fourbitbuffer_10_y2, fourbitbuffer_11_y2, fourbitbuffer_12_y2, fourbitbuffer_13_y2, fourbitbuffer_14_y2, fourbitbuffer_15_y2, fourbitbuffer_16_y2);
  or or_3 (Y1, fourbitbuffer_1_y1, fourbitbuffer_2_y1, fourbitbuffer_3_y1, fourbitbuffer_4_y1, fourbitbuffer_5_y1, fourbitbuffer_6_y1, fourbitbuffer_7_y1, fourbitbuffer_8_y1, fourbitbuffer_9_y1, fourbitbuffer_10_y1, fourbitbuffer_11_y1, fourbitbuffer_12_y1, fourbitbuffer_13_y1, fourbitbuffer_14_y1, fourbitbuffer_15_y1, fourbitbuffer_16_y1);
  or or_4 (Y0, fourbitbuffer_1_y0, fourbitbuffer_2_y0, fourbitbuffer_3_y0, fourbitbuffer_4_y0, fourbitbuffer_5_y0, fourbitbuffer_6_y0, fourbitbuffer_7_y0, fourbitbuffer_8_y0, fourbitbuffer_9_y0, fourbitbuffer_10_y0, fourbitbuffer_11_y0, fourbitbuffer_12_y0, fourbitbuffer_13_y0, fourbitbuffer_14_y0, fourbitbuffer_15_y0, fourbitbuffer_16_y0);
endmodule

module FourToSixteenDemux (
  input  S3,
  input  S2,
  input  S1,
  input  S0,
  output out_5,
  output out_6,
  output out_7,
  output out_8,
  output out_9,
  output out_10,
  output out_11,
  output out_12,
  output out_13,
  output out_14,
  output out_15,
  output out_16,
  output out_17,
  output out_18,
  output out_19,
  output out_20
);

  wire not_1_out, not_2_out, not_3_out, not_4_out, not_5_out, not_6_out, not_7_out, not_8_out, not_9_out,
       not_10_out, not_11_out, not_12_out, not_13_out, not_14_out, not_15_out, not_16_out, not_17_out,
       not_19_out, not_20_out, not_21_out, not_22_out, not_23_out, not_24_out, not_25_out, not_26_out,
       not_27_out, not_28_out, not_29_out, not_30_out, not_31_out, not_32_out;

  not not_1 (not_1_out, S3);
  not not_2 (not_2_out, S2);
  and and_1 (out_5, not_1_out, not_2_out, not_3_out, not_4_out);
  not not_3 (not_3_out, S1);
  not not_4 (not_4_out, S0);
  not not_5 (not_5_out, S3);
  not not_6 (not_6_out, S2);
  and and_2 (out_6, not_5_out, not_6_out, not_7_out, S0);
  not not_7 (not_7_out, S1);
  not not_8 (not_8_out, S3);
  not not_9 (not_9_out, S2);
  and and_3 (out_7, not_8_out, not_9_out, S1, not_10_out);
  not not_10 (not_10_out, S0);
  not not_11 (not_11_out, S3);
  not not_12 (not_12_out, S2);
  and and_4 (out_8, not_11_out, not_12_out, S1, S0);
  not not_13 (not_13_out, S3);
  and and_5 (out_9, not_13_out, S2, not_14_out, not_15_out);
  not not_14 (not_14_out, S1);
  not not_15 (not_15_out, S0);
  not not_16 (not_16_out, S3);
  and and_6 (out_10, not_16_out, S2, not_17_out, S0);
  not not_17 (not_17_out, S1);
  // NOT_Gate not_18 has open pins: in=S3, out=open
  and and_7 (out_11, S2, S1, not_19_out);
  not not_19 (not_19_out, S0);
  not not_20 (not_20_out, S3);
  and and_8 (out_12, not_20_out, S2, S1, S0);
  not not_21 (not_21_out, S2);
  and and_9 (out_13, S3, not_21_out, not_22_out, not_23_out);
  not not_22 (not_22_out, S1);
  not not_23 (not_23_out, S0);
  not not_24 (not_24_out, S2);
  and and_10 (out_14, S3, not_24_out, not_25_out, S0);
  not not_25 (not_25_out, S1);
  not not_26 (not_26_out, S2);
  and and_11 (out_15, S3, not_26_out, S1, not_27_out);
  not not_27 (not_27_out, S0);
  not not_28 (not_28_out, S2);
  and and_12 (out_16, S3, not_28_out, S1, S0);
  and and_13 (out_17, S3, S2, not_29_out, not_30_out);
  not not_29 (not_29_out, S1);
  not not_30 (not_30_out, S0);
  and and_14 (out_18, S3, S2, not_31_out, S0);
  not not_31 (not_31_out, S1);
  and and_15 (out_19, S3, S2, S1, not_32_out);
  not not_32 (not_32_out, S0);
  and and_16 (out_20, S3, S2, S1, S0);
endmodule

module ThreeBitBuffer (
  input  A2,
  input  A1,
  input  A0,
  input  S,
  output out_5,
  output out_6,
  output out_7
);

  and and_1 (out_5, A2, S);
  and and_2 (out_6, S, A1);
  and and_3 (out_7, A0, S);
endmodule

module EightToFourMux (
  input  in_1,
  input  in_2,
  input  in_3,
  input  in_4,
  input  in_5,
  input  in_6,
  input  in_7,
  input  in_8,
  input  S,
  output out_10,
  output out_11,
  output out_12,
  output out_13
);

  wire fourbitbuffer_1_y0, fourbitbuffer_1_y1, fourbitbuffer_1_y2, fourbitbuffer_1_y3, fourbitbuffer_2_y0,
       fourbitbuffer_2_y1, fourbitbuffer_2_y2, fourbitbuffer_2_y3, not_1_out;

  not not_1 (not_1_out, S);
  FourBitBuffer fourbitbuffer_1 (
    .D3(in_1), .D2(in_2), .D1(in_3), .D0(in_4), .S(not_1_out), .Y3(fourbitbuffer_1_y3),
    .Y2(fourbitbuffer_1_y2), .Y1(fourbitbuffer_1_y1), .Y0(fourbitbuffer_1_y0));
  FourBitBuffer fourbitbuffer_2 (
    .D3(in_5), .D2(in_6), .D1(in_7), .D0(in_8), .S(S), .Y3(fourbitbuffer_2_y3), .Y2(fourbitbuffer_2_y2),
    .Y1(fourbitbuffer_2_y1), .Y0(fourbitbuffer_2_y0));
  or or_1 (out_10, fourbitbuffer_1_y3, fourbitbuffer_2_y3);
  or or_2 (out_11, fourbitbuffer_1_y2, fourbitbuffer_2_y2);
  or or_3 (out_12, fourbitbuffer_1_y1, fourbitbuffer_2_y1);
  or or_4 (out_13, fourbitbuffer_1_y0, fourbitbuffer_2_y0);
endmodule

module ControlUnit (
  input  S2,
  input  S1,
  input  S0,
  input  AR,
  input  in_5,
  input  in_6,
  input  in_7,
  input  BR,
  input  in_9,
  input  in_10,
  input  in_11,
  input  XR,
  input  in_13,
  input  in_14,
  input  in_15,
  input  OPA,
  input  in_17,
  input  in_18,
  input  in_19,
  input  OPB,
  input  in_21,
  input  in_22,
  input  in_23,
  input  PC11,
  input  in_25,
  input  in_26,
  input  in_27,
  input  in_28,
  input  in_29,
  input  in_30,
  input  in_31,
  input  in_32,
  input  in_33,
  input  in_34,
  input  in_35,
  input  MD,
  input  in_37,
  input  in_38,
  input  in_39,
  input  CK,
  output AW,
  output out_42,
  output out_43,
  output out_44,
  output AWS,
  output BW,
  output out_47,
  output out_48,
  output out_49,
  output BWS,
  output MA,
  output out_52,
  output out_53,
  output out_54,
  output MW,
  output out_56,
  output out_57,
  output out_58,
  output MWS,
  output PCW11,
  output out_61,
  output out_62,
  output out_63,
  output out_64,
  output out_65,
  output out_66,
  output out_67,
  output out_68,
  output out_69,
  output out_70,
  output out_71,
  output PCW,
  output HLT
);

  wire and_1_out, and_2_out, and_3_out, d_ff_1_q, d_ff_1_qn, d_ff_2_q, fourbitadder_1_o, fourbitbuffer_2_y0,
       fourbitbuffer_2_y1, fourbitbuffer_2_y2, fourbitbuffer_2_y3, fourbitbuffer_3_y0, fourbitbuffer_3_y1,
       fourbitbuffer_3_y2, fourbitbuffer_3_y3, fourbitbuffer_5_y0, fourbitbuffer_5_y1, fourbitbuffer_5_y2,
       fourbitbuffer_5_y3, fourbitbuffer_6_y0, fourbitbuffer_6_y1, fourbitbuffer_6_y2, fourbitbuffer_6_y3,
       not_1_out, not_2_out, not_3_out, not_4_out, not_5_out, or_1_out, threetoeightdemux_1_out0,
       threetoeightdemux_1_out1, threetoeightdemux_1_out2, threetoeightdemux_1_out3,
       threetoeightdemux_1_out5, threetoeightdemux_1_out6;
  wire [3:0] fourbitadder_1_x0;
  wire [11:0] bit_extender_1_out, twelvebitbuffer_1_out_25;

  assign bit_extender_1_out = {{8{1'b0}}, fourbitadder_1_x0};  // Bit_Extender bit_extender_1
  FourBitAdder fourbitadder_1 (
    .A3(OPA), .A2(in_17), .A1(in_18), .A0(in_19), .B3(OPB), .B2(in_21), .B1(in_22), .B0(in_23),
    .O(fourbitadder_1_o), .X3(fourbitadder_1_x0[3]), .X2(fourbitadder_1_x0[2]), .X1(fourbitadder_1_x0[1]),
    .X0(fourbitadder_1_x0[0]));
  or or_1 (or_1_out, MWS, threetoeightdemux_1_out2);
  TwelveBitBuffer twelvebitbuffer_1 (
    .A11(bit_extender_1_out[11]), .in_2(bit_extender_1_out[10]), .in_3(bit_extender_1_out[9]),
    .in_4(bit_extender_1_out[8]), .in_5(bit_extender_1_out[7]), .in_6(bit_extender_1_out[6]),
    .in_7(bit_extender_1_out[5]), .in_8(fourbitadder_1_o), .in_9(bit_extender_1_out[3]),
    .in_10(bit_extender_1_out[2]), .in_11(bit_extender_1_out[1]), .in_12(bit_extender_1_out[0]), .S(PCW),
    .Y11(twelvebitbuffer_1_out_25[11]), .out_15(twelvebitbuffer_1_out_25[10]),
    .out_16(twelvebitbuffer_1_out_25[9]), .out_17(twelvebitbuffer_1_out_25[8]),
    .out_18(twelvebitbuffer_1_out_25[7]), .out_19(twelvebitbuffer_1_out_25[6]),
    .out_20(twelvebitbuffer_1_out_25[5]), .out_21(twelvebitbuffer_1_out_25[4]),
    .out_22(twelvebitbuffer_1_out_25[3]), .out_23(twelvebitbuffer_1_out_25[2]),
    .out_24(twelvebitbuffer_1_out_25[1]), .out_25(twelvebitbuffer_1_out_25[0]));
  ThreeToEightDemux threetoeightdemux_1 (
    .IN2(S2), .IN1(S1), .IN0(S0), .OUT0(threetoeightdemux_1_out0), .OUT1(threetoeightdemux_1_out1),
    .OUT2(threetoeightdemux_1_out2), .OUT3(threetoeightdemux_1_out3), .OUT4(MWS),
    .OUT5(threetoeightdemux_1_out5), .OUT6(threetoeightdemux_1_out6));  // open: OUT7
  FourBitBuffer fourbitbuffer_1 (
    .D3(XR), .D2(in_13), .D1(in_14), .D0(in_15), .S(MWS), .Y3(MW), .Y2(out_56), .Y1(out_57), .Y0(out_58));
  FourBitBuffer fourbitbuffer_2 (
    .D3(OPA), .D2(in_17), .D1(in_18), .D0(in_19), .S(threetoeightdemux_1_out1), .Y3(fourbitbuffer_2_y3),
    .Y2(fourbitbuffer_2_y2), .Y1(fourbitbuffer_2_y1), .Y0(fourbitbuffer_2_y0));
  FourBitBuffer fourbitbuffer_3 (
    .D3(OPB), .D2(in_21), .D1(in_22), .D0(in_23), .S(threetoeightdemux_1_out1), .Y3(fourbitbuffer_3_y3),
    .Y2(fourbitbuffer_3_y2), .Y1(fourbitbuffer_3_y1), .Y0(fourbitbuffer_3_y0));
  FourBitBuffer fourbitbuffer_4 (
    .D3(OPA), .D2(in_17), .D1(in_18), .D0(in_19), .S(or_1_out), .Y3(MA), .Y2(out_52), .Y1(out_53), .Y0(out_54));
  Subtractor #(.width(12)) subtractor_1 (
    .a({PC11, in_25, in_26, in_27, in_28, in_29, in_30, in_31, in_32, in_33, in_34, in_35}),
    .b(twelvebitbuffer_1_out_25),
    .out({PCW11, out_61, out_62, out_63, out_64, out_65, out_66, out_67, out_68, out_69, out_70, out_71}));  // open: bin, bout
  FourBitBuffer fourbitbuffer_5 (
    .D3(BR), .D2(in_9), .D1(in_10), .D0(in_11), .S(threetoeightdemux_1_out0), .Y3(fourbitbuffer_5_y3),
    .Y2(fourbitbuffer_5_y2), .Y1(fourbitbuffer_5_y1), .Y0(fourbitbuffer_5_y0));
  FourBitBuffer fourbitbuffer_6 (
    .D3(AR), .D2(in_5), .D1(in_6), .D0(in_7), .S(threetoeightdemux_1_out0), .Y3(fourbitbuffer_6_y3),
    .Y2(fourbitbuffer_6_y2), .Y1(fourbitbuffer_6_y1), .Y0(fourbitbuffer_6_y0));
  not not_1 (not_1_out, XR);
  not not_2 (not_2_out, in_13);
  and and_1 (and_1_out, not_1_out, not_2_out, not_3_out, not_4_out);
  not not_3 (not_3_out, in_14);
  not not_4 (not_4_out, in_15);
  and and_2 (and_2_out, threetoeightdemux_1_out5, and_1_out);
  or or_2 (PCW, and_2_out, threetoeightdemux_1_out3);
  D_Flip_Flop d_ff_1 (.D(d_ff_1_qn), .clk(and_3_out), .Q(d_ff_1_q), .Qn(d_ff_1_qn), .reset(not_5_out));  // open: preset
  and and_3 (and_3_out, threetoeightdemux_1_out2, CK);
  not not_5 (not_5_out, threetoeightdemux_1_out2);
  D_Flip_Flop d_ff_2 (
    .D(threetoeightdemux_1_out6), .clk(threetoeightdemux_1_out6), .Q(d_ff_2_q), .reset(1'b0));  // open: Qn, preset
  ThirtyTwoToFourMux thirtytwotofourmux_1 (
    .S2(S2), .S1(S1), .S0(S0), .A3(fourbitbuffer_5_y3), .in_5(fourbitbuffer_5_y2), .in_6(fourbitbuffer_5_y1),
    .A0(fourbitbuffer_5_y0), .B(fourbitbuffer_2_y3), .in_9(fourbitbuffer_2_y2), .in_10(fourbitbuffer_2_y1),
    .in_11(fourbitbuffer_2_y0), .C(MD), .in_13(in_37), .in_14(in_38), .in_15(in_39), .Y3(AW), .Y2(out_42),
    .Y1(out_43), .Y0(out_44));  // open: D, in_17, in_18, in_19, E, in_21, in_22, in_23, F, in_25, in_26, in_27, G, in_29, in_30, in_31, H, in_33, in_34, in_35
  ThirtyTwoToFourMux thirtytwotofourmux_2 (
    .S2(S2), .S1(S1), .S0(S0), .A3(fourbitbuffer_6_y3), .in_5(fourbitbuffer_6_y2), .in_6(fourbitbuffer_6_y1),
    .A0(fourbitbuffer_6_y0), .B(fourbitbuffer_3_y3), .in_9(fourbitbuffer_3_y2), .in_10(fourbitbuffer_3_y1),
    .in_11(fourbitbuffer_3_y0), .Y3(BW), .Y2(out_47), .Y1(out_48), .Y0(out_49));  // open: C, in_13, in_14, in_15, D, in_17, in_18, in_19, E, in_21, in_22, in_23, F, in_25, in_26, in_27, G, in_29, in_30, in_31, H, in_33, in_34, in_35
  or or_3 (HLT, d_ff_2_q, d_ff_1_q);
  or or_4 (AWS, threetoeightdemux_1_out1, threetoeightdemux_1_out0, threetoeightdemux_1_out2);
  or or_5 (BWS, threetoeightdemux_1_out1, threetoeightdemux_1_out0);

  // Notes on the sheet:
  //   the extender should always be in zero mode
  //   temporary fix for program jumping: add opA and opB to get up to 32 jumping backwards. still need to implement jumping forwards
  //   Note: This may need to be modified if the general memory becomes more than 16 addresses
  //   there will be two cycles to get an instruction - fixed by halting for a cycle while value is fetched 
  //   This can go to somewhere for a CONT operation.
endmodule

module SixteenToFourMux (
  input  S1,
  input  S0,
  input  A,
  input  in_4,
  input  in_5,
  input  in_6,
  input  B,
  input  in_8,
  input  in_9,
  input  in_10,
  input  C,
  input  in_12,
  input  in_13,
  input  in_14,
  input  D,
  input  in_16,
  input  in_17,
  input  in_18,
  output Y,
  output out_20,
  output out_21,
  output out_22
);

  wire and_1_out, and_2_out, and_3_out, and_4_out, fourbitbuffer_1_y0, fourbitbuffer_1_y1,
       fourbitbuffer_1_y2, fourbitbuffer_1_y3, fourbitbuffer_2_y0, fourbitbuffer_2_y1, fourbitbuffer_2_y2,
       fourbitbuffer_2_y3, fourbitbuffer_3_y0, fourbitbuffer_3_y1, fourbitbuffer_3_y2, fourbitbuffer_3_y3,
       fourbitbuffer_4_y0, fourbitbuffer_4_y1, fourbitbuffer_4_y2, fourbitbuffer_4_y3, not_1_out, not_2_out,
       not_3_out, not_4_out;

  not not_1 (not_1_out, S1);
  not not_2 (not_2_out, S0);
  not not_3 (not_3_out, S1);
  not not_4 (not_4_out, S0);
  and and_1 (and_1_out, not_1_out, not_2_out);
  and and_2 (and_2_out, not_3_out, S0);
  and and_3 (and_3_out, S1, not_4_out);
  and and_4 (and_4_out, S1, S0);
  FourBitBuffer fourbitbuffer_1 (
    .D3(A), .D2(in_4), .D1(in_5), .D0(in_6), .S(and_1_out), .Y3(fourbitbuffer_1_y3), .Y2(fourbitbuffer_1_y2),
    .Y1(fourbitbuffer_1_y1), .Y0(fourbitbuffer_1_y0));
  FourBitBuffer fourbitbuffer_2 (
    .D3(B), .D2(in_8), .D1(in_9), .D0(in_10), .S(and_2_out), .Y3(fourbitbuffer_2_y3),
    .Y2(fourbitbuffer_2_y2), .Y1(fourbitbuffer_2_y1), .Y0(fourbitbuffer_2_y0));
  FourBitBuffer fourbitbuffer_3 (
    .D3(C), .D2(in_12), .D1(in_13), .D0(in_14), .S(and_3_out), .Y3(fourbitbuffer_3_y3),
    .Y2(fourbitbuffer_3_y2), .Y1(fourbitbuffer_3_y1), .Y0(fourbitbuffer_3_y0));
  FourBitBuffer fourbitbuffer_4 (
    .D3(D), .D2(in_16), .D1(in_17), .D0(in_18), .S(and_4_out), .Y3(fourbitbuffer_4_y3),
    .Y2(fourbitbuffer_4_y2), .Y1(fourbitbuffer_4_y1), .Y0(fourbitbuffer_4_y0));
  or or_1 (Y, fourbitbuffer_1_y3, fourbitbuffer_2_y3, fourbitbuffer_3_y3, fourbitbuffer_4_y3);
  or or_2 (out_20, fourbitbuffer_1_y2, fourbitbuffer_2_y2, fourbitbuffer_3_y2, fourbitbuffer_4_y2);
  or or_3 (out_21, fourbitbuffer_1_y1, fourbitbuffer_2_y1, fourbitbuffer_3_y1, fourbitbuffer_4_y1);
  or or_4 (out_22, fourbitbuffer_1_y0, fourbitbuffer_2_y0, fourbitbuffer_3_y0, fourbitbuffer_4_y0);
endmodule

module FourBitCounter (
  input  in_1,
  input  in_2,
  input  in_3,
  input  in_4,
  input  W,
  input  CK,
  output Q0,
  output Q1,
  output Q2,
  output Q3
);

  wire d_ff_1_qn, d_ff_2_qn, d_ff_3_qn, d_ff_4_qn, fourbitbuffer_1_y0, fourbitbuffer_1_y1,
       fourbitbuffer_1_y2, fourbitbuffer_1_y3, fourbitbuffer_2_y0, fourbitbuffer_2_y1, fourbitbuffer_2_y2,
       fourbitbuffer_2_y3, not_1_out, not_2_out, not_3_out, not_4_out;

  D_Flip_Flop d_ff_1 (
    .D(d_ff_1_qn), .clk(CK), .Q(Q0), .Qn(d_ff_1_qn), .preset(fourbitbuffer_2_y0), .reset(fourbitbuffer_1_y0));
  not not_1 (not_1_out, in_1);
  not not_2 (not_2_out, in_2);
  not not_3 (not_3_out, in_3);
  not not_4 (not_4_out, in_4);
  D_Flip_Flop d_ff_2 (
    .D(d_ff_2_qn), .clk(d_ff_1_qn), .Q(Q1), .Qn(d_ff_2_qn), .preset(fourbitbuffer_2_y1),
    .reset(fourbitbuffer_1_y1));
  FourBitBuffer fourbitbuffer_1 (
    .D3(not_1_out), .D2(not_2_out), .D1(not_3_out), .D0(not_4_out), .S(W), .Y3(fourbitbuffer_1_y3),
    .Y2(fourbitbuffer_1_y2), .Y1(fourbitbuffer_1_y1), .Y0(fourbitbuffer_1_y0));
  FourBitBuffer fourbitbuffer_2 (
    .D3(in_1), .D2(in_2), .D1(in_3), .D0(in_4), .S(W), .Y3(fourbitbuffer_2_y3), .Y2(fourbitbuffer_2_y2),
    .Y1(fourbitbuffer_2_y1), .Y0(fourbitbuffer_2_y0));
  D_Flip_Flop d_ff_3 (
    .D(d_ff_3_qn), .clk(d_ff_2_qn), .Q(Q2), .Qn(d_ff_3_qn), .preset(fourbitbuffer_2_y2),
    .reset(fourbitbuffer_1_y2));
  D_Flip_Flop d_ff_4 (
    .D(d_ff_4_qn), .clk(d_ff_3_qn), .Q(Q3), .Qn(d_ff_4_qn), .preset(fourbitbuffer_2_y3),
    .reset(fourbitbuffer_1_y3));
endmodule

module TwelveBitCounter (
  input  CK,
  output out_2,
  output out_3,
  output out_4,
  output out_5,
  output out_6,
  output out_7,
  output out_8,
  output out_9,
  output out_10,
  output out_11,
  output out_12,
  output Y11,
  output out_14,
  output out_15,
  output out_16,
  output out_17,
  output out_18,
  output out_19,
  output out_20,
  output out_21,
  output out_22,
  output out_23,
  output out_24,
  output out_25
);

  wire d_ff_24_qn;

  D_Flip_Flop d_ff_1 (.D(out_3), .clk(CK), .Q(out_2), .Qn(out_3));  // open: preset, reset
  D_Flip_Flop d_ff_2 (.D(out_3), .Q(out_3), .Qn(out_3));  // open: clk, preset, reset
  D_Flip_Flop d_ff_3 (.D(out_3), .clk(out_3), .Q(out_3), .Qn(out_3));  // open: preset, reset
  D_Flip_Flop d_ff_4 (.D(out_3), .clk(out_3), .Q(out_3), .Qn(out_3));  // open: preset, reset
  D_Flip_Flop d_ff_5 (.D(out_3), .clk(out_3), .Q(out_3), .Qn(out_3));  // open: preset, reset
  D_Flip_Flop d_ff_6 (.D(out_3), .clk(out_3), .Q(out_3), .Qn(out_3));  // open: preset, reset
  D_Flip_Flop d_ff_7 (.D(out_3), .clk(out_3), .Q(out_5), .Qn(out_3), .preset(out_3));  // open: reset
  D_Flip_Flop d_ff_8 (.D(out_3), .clk(out_3), .Q(out_3), .Qn(out_3));  // open: preset, reset
  D_Flip_Flop d_ff_9 (.D(out_3), .clk(out_3), .Q(out_3), .Qn(out_3), .preset(out_3));  // open: reset
  D_Flip_Flop d_ff_10 (.D(out_3), .clk(out_3), .Q(out_3), .Qn(out_3));  // open: preset, reset
  D_Flip_Flop d_ff_11 (.D(out_3), .clk(out_3), .Q(out_3), .Qn(out_3), .preset(out_3));  // open: reset
  D_Flip_Flop d_ff_12 (.D(out_3), .clk(out_3), .Q(out_3), .Qn(out_3));  // open: preset, reset
  D_Flip_Flop d_ff_13 (.D(out_3), .clk(out_3), .Q(out_3), .Qn(out_3), .preset(out_3));  // open: reset
  D_Flip_Flop d_ff_14 (.D(out_3), .clk(out_3), .Q(out_3), .Qn(out_3));  // open: preset, reset
  D_Flip_Flop d_ff_15 (.D(out_3), .clk(out_3), .Q(out_3), .Qn(out_3), .preset(out_3));  // open: reset
  D_Flip_Flop d_ff_16 (.D(out_3), .clk(out_3), .Q(out_3), .Qn(out_3));  // open: preset, reset
  D_Flip_Flop d_ff_17 (.D(out_3), .clk(out_3), .Q(out_3), .Qn(out_3), .preset(out_3));  // open: reset
  D_Flip_Flop d_ff_18 (.D(out_3), .clk(out_3), .Q(out_3), .Qn(out_3));  // open: preset, reset
  D_Flip_Flop d_ff_19 (.D(out_3), .clk(out_3), .Q(out_3), .Qn(out_3), .preset(out_3));  // open: reset
  D_Flip_Flop d_ff_20 (.D(out_3), .clk(out_3), .Q(out_3), .Qn(out_3));  // open: preset, reset
  D_Flip_Flop d_ff_21 (.D(out_3), .clk(out_3), .Q(out_3), .Qn(out_3), .preset(out_3));  // open: reset
  D_Flip_Flop d_ff_22 (.D(out_3), .clk(out_3), .Q(out_3), .Qn(out_3));  // open: preset, reset
  D_Flip_Flop d_ff_23 (.D(out_3), .clk(out_3), .Q(Y11), .Qn(out_3), .preset(d_ff_24_qn));  // open: reset
  D_Flip_Flop d_ff_24 (.D(d_ff_24_qn), .clk(out_3), .Q(out_3), .Qn(d_ff_24_qn));  // open: preset, reset

  assign out_4 = out_3;
  assign out_6 = out_3;
  assign out_7 = out_3;
  assign out_8 = out_3;
  assign out_9 = out_3;
  assign out_10 = out_3;
  assign out_11 = out_3;
  assign out_12 = out_3;
  assign out_14 = out_3;
  assign out_15 = out_3;
  assign out_16 = out_3;
  assign out_17 = out_3;
  assign out_18 = out_3;
  assign out_19 = out_3;
  assign out_20 = out_3;
  assign out_21 = out_3;
  assign out_22 = out_3;
  assign out_23 = out_3;
  assign out_24 = out_3;
  assign out_25 = out_3;
endmodule

module ProgramCounter (
  input  S11,
  input  in_2,
  input  in_3,
  input  in_4,
  input  in_5,
  input  in_6,
  input  in_7,
  input  in_8,
  input  in_9,
  input  in_10,
  input  in_11,
  input  in_12,
  input  HALT,
  input  CK,
  input  W,
  output out_16,
  output out_17,
  output out_18,
  output out_19,
  output out_20,
  output out_21,
  output out_22,
  output out_23,
  output out_24,
  output out_25,
  output out_26,
  output Y11
);

  wire and_1_out, d_ff_1_qn, d_ff_2_qn, d_ff_3_qn, d_ff_4_qn, d_ff_5_qn, d_ff_6_qn, d_ff_7_qn, d_ff_8_qn,
       d_ff_9_qn, d_ff_10_qn, d_ff_11_qn, d_ff_12_qn, not_1_out, not_2_out, not_3_out, not_4_out, not_5_out,
       not_6_out, not_7_out, not_8_out, not_9_out, not_10_out, not_11_out, not_12_out, not_13_out,
       twelvebitbuffer_1_out_15, twelvebitbuffer_1_out_16, twelvebitbuffer_1_out_17,
       twelvebitbuffer_1_out_18, twelvebitbuffer_1_out_19, twelvebitbuffer_1_out_20,
       twelvebitbuffer_1_out_21, twelvebitbuffer_1_out_22, twelvebitbuffer_1_out_23,
       twelvebitbuffer_1_out_24, twelvebitbuffer_1_out_25, twelvebitbuffer_1_y11, twelvebitbuffer_2_out_15,
       twelvebitbuffer_2_out_16, twelvebitbuffer_2_out_17, twelvebitbuffer_2_out_18,
       twelvebitbuffer_2_out_19, twelvebitbuffer_2_out_20, twelvebitbuffer_2_out_21,
       twelvebitbuffer_2_out_22, twelvebitbuffer_2_out_23, twelvebitbuffer_2_out_24,
       twelvebitbuffer_2_out_25, twelvebitbuffer_2_y11;

  not not_1 (not_1_out, HALT);
  and and_1 (and_1_out, not_1_out, CK);
  not not_2 (not_2_out, S11);
  not not_3 (not_3_out, in_2);
  not not_4 (not_4_out, in_3);
  not not_5 (not_5_out, in_4);
  not not_6 (not_6_out, in_5);
  not not_7 (not_7_out, in_6);
  not not_8 (not_8_out, in_7);
  not not_9 (not_9_out, in_8);
  not not_10 (not_10_out, in_9);
  not not_11 (not_11_out, in_10);
  not not_12 (not_12_out, in_11);
  not not_13 (not_13_out, in_12);
  D_Flip_Flop d_ff_1 (
    .D(d_ff_1_qn), .clk(and_1_out), .Q(out_16), .Qn(d_ff_1_qn), .preset(twelvebitbuffer_1_out_25),
    .reset(twelvebitbuffer_2_out_25));
  TwelveBitBuffer twelvebitbuffer_1 (
    .A11(S11), .in_2(in_2), .in_3(in_3), .in_4(in_4), .in_5(in_5), .in_6(in_6), .in_7(in_7), .in_8(in_8),
    .in_9(in_9), .in_10(in_10), .in_11(in_11), .in_12(in_12), .S(W), .Y11(twelvebitbuffer_1_y11),
    .out_15(twelvebitbuffer_1_out_15), .out_16(twelvebitbuffer_1_out_16), .out_17(twelvebitbuffer_1_out_17),
    .out_18(twelvebitbuffer_1_out_18), .out_19(twelvebitbuffer_1_out_19), .out_20(twelvebitbuffer_1_out_20),
    .out_21(twelvebitbuffer_1_out_21), .out_22(twelvebitbuffer_1_out_22), .out_23(twelvebitbuffer_1_out_23),
    .out_24(twelvebitbuffer_1_out_24), .out_25(twelvebitbuffer_1_out_25));
  D_Flip_Flop d_ff_2 (
    .D(d_ff_2_qn), .clk(d_ff_1_qn), .Q(out_17), .Qn(d_ff_2_qn), .preset(twelvebitbuffer_1_out_24),
    .reset(twelvebitbuffer_2_out_24));
  D_Flip_Flop d_ff_3 (
    .D(d_ff_3_qn), .clk(d_ff_2_qn), .Q(out_18), .Qn(d_ff_3_qn), .preset(twelvebitbuffer_1_out_23),
    .reset(twelvebitbuffer_2_out_23));
  TwelveBitBuffer twelvebitbuffer_2 (
    .A11(not_2_out), .in_2(not_3_out), .in_3(not_4_out), .in_4(not_5_out), .in_5(not_6_out),
    .in_6(not_7_out), .in_7(not_8_out), .in_8(not_9_out), .in_9(not_10_out), .in_10(not_11_out),
    .in_11(not_12_out), .in_12(not_13_out), .S(W), .Y11(twelvebitbuffer_2_y11),
    .out_15(twelvebitbuffer_2_out_15), .out_16(twelvebitbuffer_2_out_16), .out_17(twelvebitbuffer_2_out_17),
    .out_18(twelvebitbuffer_2_out_18), .out_19(twelvebitbuffer_2_out_19), .out_20(twelvebitbuffer_2_out_20),
    .out_21(twelvebitbuffer_2_out_21), .out_22(twelvebitbuffer_2_out_22), .out_23(twelvebitbuffer_2_out_23),
    .out_24(twelvebitbuffer_2_out_24), .out_25(twelvebitbuffer_2_out_25));
  D_Flip_Flop d_ff_4 (
    .D(d_ff_4_qn), .clk(d_ff_3_qn), .Q(out_19), .Qn(d_ff_4_qn), .preset(twelvebitbuffer_1_out_22),
    .reset(twelvebitbuffer_2_out_22));
  D_Flip_Flop d_ff_5 (
    .D(d_ff_5_qn), .clk(d_ff_4_qn), .Q(out_20), .Qn(d_ff_5_qn), .preset(twelvebitbuffer_1_out_21),
    .reset(twelvebitbuffer_2_out_21));
  D_Flip_Flop d_ff_6 (
    .D(d_ff_6_qn), .clk(d_ff_5_qn), .Q(out_21), .Qn(d_ff_6_qn), .preset(twelvebitbuffer_1_out_20),
    .reset(twelvebitbuffer_2_out_20));
  D_Flip_Flop d_ff_7 (
    .D(d_ff_7_qn), .clk(d_ff_6_qn), .Q(out_22), .Qn(d_ff_7_qn), .preset(twelvebitbuffer_1_out_19),
    .reset(twelvebitbuffer_2_out_19));
  D_Flip_Flop d_ff_8 (
    .D(d_ff_8_qn), .clk(d_ff_7_qn), .Q(out_23), .Qn(d_ff_8_qn), .preset(twelvebitbuffer_1_out_18),
    .reset(twelvebitbuffer_2_out_18));
  D_Flip_Flop d_ff_9 (
    .D(d_ff_9_qn), .clk(d_ff_8_qn), .Q(out_24), .Qn(d_ff_9_qn), .preset(twelvebitbuffer_1_out_17),
    .reset(twelvebitbuffer_2_out_17));
  D_Flip_Flop d_ff_10 (
    .D(d_ff_10_qn), .clk(d_ff_9_qn), .Q(out_25), .Qn(d_ff_10_qn), .preset(twelvebitbuffer_1_out_16),
    .reset(twelvebitbuffer_2_out_16));
  D_Flip_Flop d_ff_11 (
    .D(d_ff_11_qn), .clk(d_ff_10_qn), .Q(out_26), .Qn(d_ff_11_qn), .preset(twelvebitbuffer_1_out_15),
    .reset(twelvebitbuffer_2_out_15));
  D_Flip_Flop d_ff_12 (
    .D(d_ff_12_qn), .clk(d_ff_11_qn), .Q(Y11), .Qn(d_ff_12_qn), .preset(twelvebitbuffer_1_y11),
    .reset(twelvebitbuffer_2_y11));
endmodule

module TwelveBitBuffer (
  input  A11,
  input  in_2,
  input  in_3,
  input  in_4,
  input  in_5,
  input  in_6,
  input  in_7,
  input  in_8,
  input  in_9,
  input  in_10,
  input  in_11,
  input  in_12,
  input  S,
  output Y11,
  output out_15,
  output out_16,
  output out_17,
  output out_18,
  output out_19,
  output out_20,
  output out_21,
  output out_22,
  output out_23,
  output out_24,
  output out_25
);

  and and_1 (Y11, S, A11);
  and and_2 (out_15, S, in_2);
  and and_3 (out_16, S, in_3);
  and and_4 (out_17, S, in_4);
  and and_5 (out_18, S, in_5);
  and and_6 (out_19, S, in_6);
  and and_7 (out_20, S, in_7);
  and and_8 (out_21, S, in_8);
  and and_9 (out_22, S, in_9);
  and and_10 (out_23, S, in_10);
  and and_11 (out_24, S, in_11);
  and and_12 (out_25, S, in_12);
endmodule

module TwelveBitRegister (
  input  W11,
  input  in_2,
  input  in_3,
  input  in_4,
  input  in_5,
  input  in_6,
  input  in_7,
  input  in_8,
  input  in_9,
  input  in_10,
  input  in_11,
  input  in_12,
  input  W,
  input  CK,
  output D11,
  output out_16,
  output out_17,
  output out_18,
  output out_19,
  output out_20,
  output out_21,
  output out_22,
  output out_23,
  output out_24,
  output out_25,
  output out_26
);

  wire and_1_out, twelvebitbuffer_1_out_15, twelvebitbuffer_1_out_16, twelvebitbuffer_1_out_17,
       twelvebitbuffer_1_out_18, twelvebitbuffer_1_out_19, twelvebitbuffer_1_out_20,
       twelvebitbuffer_1_out_21, twelvebitbuffer_1_out_22, twelvebitbuffer_1_out_23,
       twelvebitbuffer_1_out_24, twelvebitbuffer_1_out_25, twelvebitbuffer_1_y11;

  TwelveBitBuffer twelvebitbuffer_1 (
    .A11(W11), .in_2(in_2), .in_3(in_3), .in_4(in_4), .in_5(in_5), .in_6(in_6), .in_7(in_7), .in_8(in_8),
    .in_9(in_9), .in_10(in_10), .in_11(in_11), .in_12(in_12), .S(W), .Y11(twelvebitbuffer_1_y11),
    .out_15(twelvebitbuffer_1_out_15), .out_16(twelvebitbuffer_1_out_16), .out_17(twelvebitbuffer_1_out_17),
    .out_18(twelvebitbuffer_1_out_18), .out_19(twelvebitbuffer_1_out_19), .out_20(twelvebitbuffer_1_out_20),
    .out_21(twelvebitbuffer_1_out_21), .out_22(twelvebitbuffer_1_out_22), .out_23(twelvebitbuffer_1_out_23),
    .out_24(twelvebitbuffer_1_out_24), .out_25(twelvebitbuffer_1_out_25));
  and and_1 (and_1_out, W, CK);
  DataStore datastore_1 (
    .A3(twelvebitbuffer_1_y11), .A2(twelvebitbuffer_1_out_15), .A1(twelvebitbuffer_1_out_16),
    .A0(twelvebitbuffer_1_out_17), .CK(and_1_out), .Y3(D11), .Y2(out_16), .Y1(out_17), .Y0(out_18));
  DataStore datastore_2 (
    .A3(twelvebitbuffer_1_out_18), .A2(twelvebitbuffer_1_out_19), .A1(twelvebitbuffer_1_out_20),
    .A0(twelvebitbuffer_1_out_21), .CK(and_1_out), .Y3(out_19), .Y2(out_20), .Y1(out_21), .Y0(out_22));
  DataStore datastore_3 (
    .A3(twelvebitbuffer_1_out_22), .A2(twelvebitbuffer_1_out_23), .A1(twelvebitbuffer_1_out_24),
    .A0(twelvebitbuffer_1_out_25), .CK(and_1_out), .Y3(out_23), .Y2(out_24), .Y1(out_25), .Y0(out_26));
endmodule

module FourBitMultiplier (
  input  in_1,
  input  in_2,
  input  in_3,
  input  in_4,
  input  [3:0] in_5,
  output out_6,
  output out_7,
  output out_8,
  output out_9
);

  wire fourbitadder_1_x0, fourbitadder_1_x1, fourbitadder_1_x2, fourbitadder_1_x3, fourbitadder_2_x0,
       fourbitadder_2_x1, fourbitadder_2_x2, fourbitadder_2_x3;
  wire [3:0] singlelinebuffer_1_oup, singlelinebuffer_2_oup, singlelinebuffer_3_oup, singlelinebuffer_4_oup;

  SingleLineBuffer singlelinebuffer_1 (.S(in_1), .INP(in_5), .OUP(singlelinebuffer_1_oup));
  SingleLineBuffer singlelinebuffer_2 (.S(in_2), .INP(in_5), .OUP(singlelinebuffer_2_oup));
  SingleLineBuffer singlelinebuffer_3 (.S(in_3), .INP(in_5), .OUP(singlelinebuffer_3_oup));
  SingleLineBuffer singlelinebuffer_4 (.S(in_4), .INP(in_5), .OUP(singlelinebuffer_4_oup));
  FourBitAdder fourbitadder_1 (
    .A3(singlelinebuffer_1_oup[3]), .A2(singlelinebuffer_1_oup[1]), .A1(singlelinebuffer_1_oup[2]),
    .A0(singlelinebuffer_1_oup[0]), .B3(singlelinebuffer_2_oup[3]), .B2(singlelinebuffer_2_oup[1]),
    .B1(singlelinebuffer_2_oup[2]), .B0(singlelinebuffer_2_oup[0]), .X3(fourbitadder_1_x3),
    .X2(fourbitadder_1_x2), .X1(fourbitadder_1_x1), .X0(fourbitadder_1_x0));  // open: O
  FourBitAdder fourbitadder_2 (
    .A3(singlelinebuffer_3_oup[3]), .A2(singlelinebuffer_3_oup[1]), .A1(singlelinebuffer_3_oup[2]),
    .A0(singlelinebuffer_3_oup[0]), .B3(singlelinebuffer_4_oup[3]), .B2(singlelinebuffer_4_oup[1]),
    .B1(singlelinebuffer_4_oup[2]), .B0(singlelinebuffer_4_oup[0]), .X3(fourbitadder_2_x3),
    .X2(fourbitadder_2_x2), .X1(fourbitadder_2_x1), .X0(fourbitadder_2_x0));  // open: O
  FourBitAdder fourbitadder_3 (
    .A3(fourbitadder_1_x3), .A2(fourbitadder_1_x2), .A1(fourbitadder_1_x1), .A0(fourbitadder_1_x0),
    .B3(fourbitadder_2_x3), .B2(fourbitadder_2_x2), .B1(fourbitadder_2_x1), .B0(fourbitadder_2_x0),
    .X3(out_6), .X2(out_7), .X1(out_8), .X0(out_9));  // open: O
endmodule

module SingleLineBuffer (
  input  S,
  input  [3:0] INP,
  output [3:0] OUP
);

  and and_1 (OUP[0], INP[0], S);
  and and_2 (OUP[1], INP[1], S);
  and and_3 (OUP[2], INP[2], S);
  and and_4 (OUP[3], INP[3], S);
endmodule
