// Logisim project Testing.circ as structural Verilog: 2 circuits, main circuit main
module main (
  input  in_1
);

  // AND_Gate and_1 is placed but not wired
endmodule

module Gates (
  input  A,
  input  B
);

  // AND_Gate and_1 has open pins: in0=A, in1=B, out=open
endmodule
